// Logisim project Addere.circ as structural Verilog
module main (
  input  in_1,
  input  in_2,
  input  in_3,
  input  in_4,
  input  in_5,
  input  in_6,
  input  in_7,
  input  in_8,
  input  in_9,
  input  in_10,
  input  in_11,
  input  in_12,
  input  in_13,
  input  in_14,
  output out_15,
  output out_16,
  output out_17,
  output out_18,
  output out_19,
  output out_20,
  output out_21,
  output out_22,
  output OutCarry
);

  wire and_2_out, and_3_out, and_4_out, and_5_out, and_6_out, and_7_out, and_8_out, and_9_out, and_10_out,
       and_11_out, or_2_out, or_3_out, or_4_out, xor_2_out, xor_4_out, xor_5_out, xor_6_out, xor_7_out;

  xor xor_1 (out_15, in_1, in_2);
  and and_1 (out_16, in_1, in_2);
  xor xor_2 (xor_2_out, in_12, in_13);
  and and_2 (and_2_out, in_13, in_12);
  and and_3 (and_3_out, xor_2_out, in_14);
  xor xor_3 (out_22, xor_2_out, in_14);
  or or_1 (OutCarry, and_2_out, and_3_out);
  xor xor_4 (xor_4_out, in_4, in_5);
  and and_4 (and_4_out, in_5, in_4);
  xor xor_5 (xor_5_out, in_6, in_7);
  and and_5 (and_5_out, in_7, in_6);
  xor xor_6 (xor_6_out, in_8, in_9);
  and and_6 (and_6_out, in_9, in_8);
  xor xor_7 (xor_7_out, in_10, in_11);
  and and_7 (and_7_out, in_11, in_10);
  and and_8 (and_8_out, xor_4_out, in_3);
  and and_9 (and_9_out, xor_5_out, or_2_out);
  and and_10 (and_10_out, xor_6_out, or_3_out);
  and and_11 (and_11_out, xor_7_out, or_4_out);
  xor xor_8 (out_17, xor_4_out, in_3);
  or or_2 (or_2_out, and_4_out, and_8_out);
  xor xor_9 (out_18, xor_5_out, or_2_out);
  or or_3 (or_3_out, and_5_out, and_9_out);
  xor xor_10 (out_19, xor_6_out, or_3_out);
  or or_4 (or_4_out, and_6_out, and_10_out);
  xor xor_11 (out_20, xor_7_out, or_4_out);
  or or_5 (out_21, and_7_out, and_11_out);

  // Notes on the sheet:
  //   b: 11 + 01 =100
  //   A
  //   B
  //   InCarry
  //   Sum
  //   Carry
  //   Sum
  //   C1
  //   C1
  //   Sum
  //   C2
  //   Sum
  //   Sum
  //   Sum
  //   C2
  //   C2
  //   C2
endmodule

module halfadder (
  input  in_1,
  input  in_2,
  output out_3,
  output out_4
);

  xor xor_1 (out_3, in_1, in_2);
  and and_1 (out_4, in_1, in_2);

  // Notes on the sheet:
  //   S
  //   C
endmodule

module fulladder (
  input  in_1,
  input  in_2,
  input  in_3,
  output out_4,
  output OutCarry
);

  wire and_1_out, and_2_out, xor_1_out;

  xor xor_1 (xor_1_out, in_1, in_2);
  and and_1 (and_1_out, in_2, in_1);
  and and_2 (and_2_out, xor_1_out, in_3);
  xor xor_2 (out_4, xor_1_out, in_3);
  or or_1 (OutCarry, and_1_out, and_2_out);

  // Notes on the sheet:
  //   A
  //   B
  //   Sum
endmodule

module fulladder_36 (
  input  in_1,
  input  in_2,
  input  in_3,
  input  in_4,
  input  in_5,
  input  in_6,
  output out_7,
  output out_8,
  output Sum,
  output Count
);

  wire halfadder_1_out_3, halfadder_1_out_4, halfadder_2_out_4, halfadder_3_out_4, halfadder_4_out_3,
       halfadder_4_out_4, or_3_out;

  halfadder halfadder_1 (.in_1(in_4), .in_2(in_5), .out_3(halfadder_1_out_3), .out_4(halfadder_1_out_4));
  halfadder halfadder_2 (.in_1(halfadder_1_out_3), .in_2(in_6), .out_3(Sum), .out_4(halfadder_2_out_4));
  or or_1 (Count, halfadder_2_out_4, halfadder_1_out_4);
  halfadder halfadder_3 (.in_1(in_1), .in_2(in_2), .out_3(out_7), .out_4(halfadder_3_out_4));
  halfadder halfadder_4 (.in_1(halfadder_3_out_4), .in_2(in_3), .out_3(halfadder_4_out_3), .out_4(halfadder_4_out_4));
  or or_2 (out_8, halfadder_4_out_3, halfadder_4_out_4);
  or or_3 (or_3_out, halfadder_4_out_4, halfadder_4_out_3);

  // Notes on the sheet:
  //   But this is not a #T(36) fulladder, this is just a fulladder made of two  halfadder
endmodule

module adder_4bits (
);

  wire decoder_7segments_i_1_out_5, decoder_7segments_i_1_out_6, decoder_7segments_i_1_out_7,
       decoder_7segments_i_1_out_8, decoder_7segments_i_1_out_9, decoder_7segments_i_1_out_10,
       decoder_7segments_i_1_out_11, decoder_7segments_i_2_out_5, decoder_7segments_i_2_out_6,
       decoder_7segments_i_2_out_7, decoder_7segments_i_2_out_8, decoder_7segments_i_2_out_9,
       decoder_7segments_i_2_out_10, decoder_7segments_i_2_out_11, decoder_7segments_i_3_out_5,
       decoder_7segments_i_3_out_6, decoder_7segments_i_3_out_7, decoder_7segments_i_3_out_8,
       decoder_7segments_i_3_out_9, decoder_7segments_i_3_out_10, decoder_7segments_i_3_out_11,
       dipswitch_1_sw1, dipswitch_1_sw2, dipswitch_1_sw3, dipswitch_1_sw4, dipswitch_2_sw1, dipswitch_2_sw2,
       dipswitch_2_sw3, dipswitch_2_sw4, fulladder_1_out_4, fulladder_1_outcarry, fulladder_2_out_4,
       fulladder_2_outcarry, fulladder_3_out_4, fulladder_3_outcarry, fulladder_4_out_4, fulladder_4_outcarry;

  DipSwitch dipswitch_1 (
    .sw1(dipswitch_1_sw1), .sw2(dipswitch_1_sw2), .sw3(dipswitch_1_sw3), .sw4(dipswitch_1_sw4));  // open: sw5, sw6, sw7, sw8
  DipSwitch dipswitch_2 (
    .sw1(dipswitch_2_sw1), .sw2(dipswitch_2_sw2), .sw3(dipswitch_2_sw3), .sw4(dipswitch_2_sw4));  // open: sw5, sw6, sw7, sw8
  decoder_7segments_i decoder_7segments_i_1 (
    .in_1(dipswitch_1_sw1), .in_2(dipswitch_1_sw2), .in_3(dipswitch_1_sw3), .in_4(dipswitch_1_sw4),
    .out_5(decoder_7segments_i_1_out_5), .out_6(decoder_7segments_i_1_out_6),
    .out_7(decoder_7segments_i_1_out_7), .out_8(decoder_7segments_i_1_out_8),
    .out_9(decoder_7segments_i_1_out_9), .out_10(decoder_7segments_i_1_out_10),
    .out_11(decoder_7segments_i_1_out_11));
  decoder_7segments_i decoder_7segments_i_2 (
    .in_1(dipswitch_2_sw1), .in_2(dipswitch_2_sw2), .in_3(dipswitch_2_sw3), .in_4(dipswitch_2_sw4),
    .out_5(decoder_7segments_i_2_out_5), .out_6(decoder_7segments_i_2_out_6),
    .out_7(decoder_7segments_i_2_out_7), .out_8(decoder_7segments_i_2_out_8),
    .out_9(decoder_7segments_i_2_out_9), .out_10(decoder_7segments_i_2_out_10),
    .out_11(decoder_7segments_i_2_out_11));
  _7_Segment_Display u_7_segment_display_1 (
    .g(decoder_7segments_i_1_out_5), .f(decoder_7segments_i_1_out_6), .a(decoder_7segments_i_1_out_7),
    .b(decoder_7segments_i_1_out_8), .e(decoder_7segments_i_1_out_9), .d(decoder_7segments_i_1_out_10),
    .c(decoder_7segments_i_1_out_11));  // open: dp
  _7_Segment_Display u_7_segment_display_2 (
    .g(decoder_7segments_i_2_out_5), .f(decoder_7segments_i_2_out_6), .a(decoder_7segments_i_2_out_7),
    .b(decoder_7segments_i_2_out_8), .e(decoder_7segments_i_2_out_9), .d(decoder_7segments_i_2_out_10),
    .c(decoder_7segments_i_2_out_11));  // open: dp
  fulladder fulladder_1 (
    .in_1(dipswitch_1_sw1), .in_2(dipswitch_2_sw1), .in_3(1'b0), .out_4(fulladder_1_out_4),
    .OutCarry(fulladder_1_outcarry));
  fulladder fulladder_2 (
    .in_1(dipswitch_1_sw2), .in_2(dipswitch_2_sw2), .in_3(fulladder_1_outcarry), .out_4(fulladder_2_out_4),
    .OutCarry(fulladder_2_outcarry));
  fulladder fulladder_3 (
    .in_1(dipswitch_1_sw3), .in_2(dipswitch_2_sw3), .in_3(fulladder_2_outcarry), .out_4(fulladder_3_out_4),
    .OutCarry(fulladder_3_outcarry));
  fulladder fulladder_4 (
    .in_1(dipswitch_1_sw4), .in_2(dipswitch_2_sw4), .in_3(fulladder_3_outcarry), .out_4(fulladder_4_out_4),
    .OutCarry(fulladder_4_outcarry));
  decoder_7segments_i decoder_7segments_i_3 (
    .in_1(fulladder_1_out_4), .in_2(fulladder_2_out_4), .in_3(fulladder_3_out_4), .in_4(fulladder_4_out_4),
    .out_5(decoder_7segments_i_3_out_5), .out_6(decoder_7segments_i_3_out_6),
    .out_7(decoder_7segments_i_3_out_7), .out_8(decoder_7segments_i_3_out_8),
    .out_9(decoder_7segments_i_3_out_9), .out_10(decoder_7segments_i_3_out_10),
    .out_11(decoder_7segments_i_3_out_11));
  _7_Segment_Display u_7_segment_display_3 (
    .g(decoder_7segments_i_3_out_5), .f(decoder_7segments_i_3_out_6), .a(decoder_7segments_i_3_out_7),
    .b(decoder_7segments_i_3_out_8), .e(decoder_7segments_i_3_out_9), .d(decoder_7segments_i_3_out_10),
    .c(decoder_7segments_i_3_out_11));  // open: dp
  LED led_1 (.in(fulladder_4_outcarry));
endmodule

module DECODER2_4 (
  input  B,
  input  in_2,
  output out_3,
  output out_4,
  output out_5,
  output out_6
);

  wire not_1_out, not_2_out, not_3_out;

  not not_1 (not_1_out, in_2);
  not not_2 (not_2_out, B);
  not not_3 (not_3_out, B);
  and and_1 (out_3, not_1_out, not_2_out);
  and and_2 (out_4, not_1_out, B);
  and and_3 (out_5, in_2, not_3_out);
  and and_4 (out_6, in_2, B);

  // Notes on the sheet:
  //   A
endmodule

module decoder3_8 (
  input  in_1,
  input  in_2,
  input  in_3,
  output out_4,
  output out_5,
  output out_6,
  output out_7,
  output out_8,
  output out_9,
  output out_10,
  output out_11
);

  wire not_1_out, not_2_out, not_3_out;

  not not_1 (not_1_out, in_1);
  not not_2 (not_2_out, in_2);
  not not_3 (not_3_out, in_3);
  and and_1 (out_4, not_1_out, not_2_out, not_3_out);
  and and_2 (out_5, in_1, not_2_out, not_3_out);
  and and_3 (out_6, not_1_out, in_2, not_3_out);
  and and_4 (out_7, in_1, in_2, not_3_out);
  and and_5 (out_8, not_1_out, not_2_out, in_3);
  and and_6 (out_9, in_1, not_2_out, in_3);
  and and_7 (out_10, not_1_out, in_2, in_3);
  and and_8 (out_11, in_1, in_2, in_3);
endmodule

module decoder4_16 (
  input  in_1,
  input  in_2,
  input  in_3,
  input  in_4,
  output out_5,
  output out_6,
  output out_7,
  output out_8,
  output out_9,
  output out_10,
  output out_11,
  output out_12,
  output out_13,
  output out_14,
  output out_15,
  output out_16,
  output out_17,
  output out_18,
  output out_19,
  output out_20
);

  wire and_1_out, and_2_out, and_3_out, and_4_out, and_5_out, and_6_out, decoder3_8_1_out_4,
       decoder3_8_2_out_4, not_1_out;

  not not_1 (not_1_out, in_4);
  and and_1 (and_1_out, in_1, not_1_out);
  and and_2 (and_2_out, in_2, not_1_out);
  and and_3 (and_3_out, in_3, not_1_out);
  and and_4 (and_4_out, in_4, in_1);
  and and_5 (and_5_out, in_4, in_2);
  and and_6 (and_6_out, in_4, in_3);
  decoder3_8 decoder3_8_1 (
    .in_1(and_1_out), .in_2(and_2_out), .in_3(and_3_out), .out_4(decoder3_8_1_out_4), .out_5(out_6),
    .out_6(out_7), .out_7(out_8), .out_8(out_9), .out_9(out_10), .out_10(out_11), .out_11(out_12));
  decoder3_8 decoder3_8_2 (
    .in_1(and_4_out), .in_2(and_5_out), .in_3(and_6_out), .out_4(decoder3_8_2_out_4), .out_5(out_14),
    .out_6(out_15), .out_7(out_16), .out_8(out_17), .out_9(out_18), .out_10(out_19), .out_11(out_20));
  and and_7 (out_5, not_1_out, decoder3_8_1_out_4);
  and and_8 (out_13, in_4, decoder3_8_2_out_4);
endmodule

module decoder_7segments (
  input  in_1,
  input  in_2,
  input  in_3,
  input  in_4,
  output out_5,
  output out_6,
  output out_7,
  output out_8,
  output out_9,
  output out_10,
  output out_11,
  output out_12
);

  wire button_1_out, button_2_out, button_3_out, button_4_out, button_5_out, button_6_out, button_7_out,
       button_8_out, decoder4_16_1_out_5, decoder4_16_1_out_6, decoder4_16_1_out_7, decoder4_16_1_out_8,
       decoder4_16_1_out_9, decoder4_16_1_out_10, decoder4_16_1_out_11, decoder4_16_1_out_12,
       decoder4_16_1_out_13, decoder4_16_1_out_14, not_1_out, not_2_out, not_3_out, not_4_out, not_5_out,
       not_6_out, not_7_out, not_8_out, not_9_out, not_10_out;

  Button button_1 (.out(button_1_out));
  Button button_2 (.out(button_2_out));
  Button button_3 (.out(button_3_out));
  Button button_4 (.out(button_4_out));
  Button button_5 (.out(button_5_out));
  Button button_6 (.out(button_6_out));
  Button button_7 (.out(button_7_out));
  Button button_8 (.out(button_8_out));
  _7_Segment_Display u_7_segment_display_1 (
    .g(button_4_out), .f(button_3_out), .a(button_2_out), .b(button_1_out), .e(button_5_out),
    .d(button_6_out), .c(button_7_out), .dp(button_8_out));
  decoder4_16 decoder4_16_1 (
    .in_1(in_1), .in_2(in_2), .in_3(in_3), .in_4(in_4), .out_5(decoder4_16_1_out_5),
    .out_6(decoder4_16_1_out_6), .out_7(decoder4_16_1_out_7), .out_8(decoder4_16_1_out_8),
    .out_9(decoder4_16_1_out_9), .out_10(decoder4_16_1_out_10), .out_11(decoder4_16_1_out_11),
    .out_12(decoder4_16_1_out_12), .out_13(decoder4_16_1_out_13), .out_14(decoder4_16_1_out_14));  // open: out_15, out_16, out_17, out_18, out_19, out_20
  or or_1 (out_5, decoder4_16_1_out_7, decoder4_16_1_out_8, decoder4_16_1_out_9, decoder4_16_1_out_10, decoder4_16_1_out_11, decoder4_16_1_out_13, decoder4_16_1_out_14);
  or or_2 (out_6, decoder4_16_1_out_5, decoder4_16_1_out_9, decoder4_16_1_out_10, decoder4_16_1_out_11, decoder4_16_1_out_13, decoder4_16_1_out_14);
  or or_3 (out_7, decoder4_16_1_out_5, decoder4_16_1_out_7, decoder4_16_1_out_8, decoder4_16_1_out_10, decoder4_16_1_out_11, decoder4_16_1_out_12, decoder4_16_1_out_13, decoder4_16_1_out_14);
  or or_4 (out_11, decoder4_16_1_out_5, decoder4_16_1_out_7, decoder4_16_1_out_8, decoder4_16_1_out_10, decoder4_16_1_out_11, decoder4_16_1_out_13, decoder4_16_1_out_14);
  or or_5 (out_8, decoder4_16_1_out_5, decoder4_16_1_out_6, decoder4_16_1_out_7, decoder4_16_1_out_8, decoder4_16_1_out_9, decoder4_16_1_out_12, decoder4_16_1_out_13, decoder4_16_1_out_14);
  or or_6 (out_12, decoder4_16_1_out_5, decoder4_16_1_out_7, decoder4_16_1_out_11, decoder4_16_1_out_13);
  not not_1 (not_1_out, decoder4_16_1_out_5);
  not not_2 (not_2_out, decoder4_16_1_out_6);
  not not_3 (not_3_out, decoder4_16_1_out_7);
  not not_4 (not_4_out, decoder4_16_1_out_8);
  not not_5 (not_5_out, decoder4_16_1_out_9);
  not not_6 (not_6_out, decoder4_16_1_out_10);
  not not_7 (not_7_out, decoder4_16_1_out_11);
  not not_8 (not_8_out, decoder4_16_1_out_12);
  not not_9 (not_9_out, decoder4_16_1_out_13);
  not not_10 (not_10_out, decoder4_16_1_out_14);
  or or_7 (out_10, decoder4_16_1_out_5, decoder4_16_1_out_6, decoder4_16_1_out_13, decoder4_16_1_out_8, decoder4_16_1_out_14, decoder4_16_1_out_9, decoder4_16_1_out_10, decoder4_16_1_out_11, decoder4_16_1_out_12);
  and and_1 (out_9, not_1_out, not_2_out, not_3_out, not_4_out, not_5_out, not_6_out, not_7_out, not_8_out, not_9_out, not_10_out);
  _7_Segment_Display u_7_segment_display_2 (
    .g(out_5), .f(out_6), .a(out_7), .b(out_8), .e(out_12), .d(out_11), .c(out_10), .dp(out_9));

  // Notes on the sheet:
  //   0
  //   1
  //   2
  //   3
  //   4
  //   5
  //   6
  //   7
  //   8
  //   9
endmodule

module decoder_7segments_i (
  input  in_1,
  input  in_2,
  input  in_3,
  input  in_4,
  output out_5,
  output out_6,
  output out_7,
  output out_8,
  output out_9,
  output out_10,
  output out_11
);

  wire button_1_out, button_2_out, button_3_out, button_4_out, button_5_out, button_6_out, button_7_out,
       button_8_out, decoder4_16_1_out_5, decoder4_16_1_out_6, decoder4_16_1_out_7, decoder4_16_1_out_8,
       decoder4_16_1_out_9, decoder4_16_1_out_10, decoder4_16_1_out_11, decoder4_16_1_out_12,
       decoder4_16_1_out_13, decoder4_16_1_out_14, decoder4_16_1_out_15, decoder4_16_1_out_16,
       decoder4_16_1_out_17, decoder4_16_1_out_18, decoder4_16_1_out_19, decoder4_16_1_out_20;

  decoder4_16 decoder4_16_1 (
    .in_1(in_1), .in_2(in_2), .in_3(in_3), .in_4(in_4), .out_5(decoder4_16_1_out_5),
    .out_6(decoder4_16_1_out_6), .out_7(decoder4_16_1_out_7), .out_8(decoder4_16_1_out_8),
    .out_9(decoder4_16_1_out_9), .out_10(decoder4_16_1_out_10), .out_11(decoder4_16_1_out_11),
    .out_12(decoder4_16_1_out_12), .out_13(decoder4_16_1_out_13), .out_14(decoder4_16_1_out_14),
    .out_15(decoder4_16_1_out_15), .out_16(decoder4_16_1_out_16), .out_17(decoder4_16_1_out_17),
    .out_18(decoder4_16_1_out_18), .out_19(decoder4_16_1_out_19), .out_20(decoder4_16_1_out_20));
  or or_1 (out_5, decoder4_16_1_out_7, decoder4_16_1_out_8, decoder4_16_1_out_9, decoder4_16_1_out_10, decoder4_16_1_out_11, decoder4_16_1_out_13, decoder4_16_1_out_14, decoder4_16_1_out_15, decoder4_16_1_out_16, decoder4_16_1_out_18, decoder4_16_1_out_19, decoder4_16_1_out_20);
  or or_2 (out_6, decoder4_16_1_out_5, decoder4_16_1_out_9, decoder4_16_1_out_10, decoder4_16_1_out_11, decoder4_16_1_out_13, decoder4_16_1_out_14, decoder4_16_1_out_15, decoder4_16_1_out_16, decoder4_16_1_out_17, decoder4_16_1_out_19, decoder4_16_1_out_20);
  or or_3 (out_7, decoder4_16_1_out_5, decoder4_16_1_out_7, decoder4_16_1_out_8, decoder4_16_1_out_10, decoder4_16_1_out_11, decoder4_16_1_out_12, decoder4_16_1_out_13, decoder4_16_1_out_14, decoder4_16_1_out_15, decoder4_16_1_out_17, decoder4_16_1_out_19, decoder4_16_1_out_20);
  or or_4 (out_8, decoder4_16_1_out_5, decoder4_16_1_out_6, decoder4_16_1_out_7, decoder4_16_1_out_8, decoder4_16_1_out_9, decoder4_16_1_out_12, decoder4_16_1_out_13, decoder4_16_1_out_14, decoder4_16_1_out_15, decoder4_16_1_out_18);
  or or_5 (out_9, decoder4_16_1_out_5, decoder4_16_1_out_7, decoder4_16_1_out_11, decoder4_16_1_out_13, decoder4_16_1_out_20, decoder4_16_1_out_15, decoder4_16_1_out_16, decoder4_16_1_out_17, decoder4_16_1_out_18, decoder4_16_1_out_19);
  or or_6 (out_10, decoder4_16_1_out_5, decoder4_16_1_out_7, decoder4_16_1_out_8, decoder4_16_1_out_10, decoder4_16_1_out_11, decoder4_16_1_out_13, decoder4_16_1_out_14, decoder4_16_1_out_16, decoder4_16_1_out_17, decoder4_16_1_out_18, decoder4_16_1_out_19);
  or or_7 (out_11, decoder4_16_1_out_5, decoder4_16_1_out_6, decoder4_16_1_out_8, decoder4_16_1_out_9, decoder4_16_1_out_10, decoder4_16_1_out_11, decoder4_16_1_out_12, decoder4_16_1_out_13, decoder4_16_1_out_14, decoder4_16_1_out_15, decoder4_16_1_out_16, decoder4_16_1_out_18);
  _7_Segment_Display u_7_segment_display_1 (
    .g(out_5), .f(out_6), .a(out_7), .b(out_8), .e(out_9), .d(out_10), .c(out_11));  // open: dp
  Button button_1 (.out(button_1_out));
  Button button_2 (.out(button_2_out));
  Button button_3 (.out(button_3_out));
  Button button_4 (.out(button_4_out));
  _7_Segment_Display u_7_segment_display_2 (
    .g(button_4_out), .f(button_3_out), .a(button_2_out), .b(button_1_out), .e(button_5_out),
    .d(button_6_out), .c(button_7_out), .dp(button_8_out));
  Button button_5 (.out(button_5_out));
  Button button_6 (.out(button_6_out));
  Button button_7 (.out(button_7_out));
  Button button_8 (.out(button_8_out));

  // Notes on the sheet:
  //    0
  //   1
  //   2
  //   3
  //   4
  //   5
  //   6
  //   7
  //   8
  //   9
  //   A
  //   b
  //   C
  //   d
  //   E
  //   F
endmodule

module main_1 (
  input  in_1,
  input  in_2,
  input  in_3,
  output out_4,
  output out_5,
  output out_6,
  output out_7
);

  wire clock_1_out, clock_2_out, clock_3_out, clock_4_out, clock_5_out, decoder2_4_1_out_3,
       decoder2_4_1_out_4, decoder2_4_1_out_5, decoder2_4_1_out_6, decoder2_4_2_out_3, decoder2_4_2_out_4,
       decoder2_4_2_out_5, decoder2_4_2_out_6, decoder2_4_3_out_3, decoder2_4_3_out_4, decoder2_4_3_out_5,
       decoder2_4_3_out_6, decoder4_16_1_out_5, decoder4_16_1_out_6, decoder4_16_1_out_7,
       decoder4_16_1_out_8, decoder4_16_1_out_9, decoder4_16_1_out_10, decoder4_16_1_out_11,
       decoder4_16_1_out_12, decoder4_16_1_out_13, decoder4_16_1_out_14, decoder4_16_1_out_15,
       decoder4_16_1_out_16, decoder4_16_1_out_17, decoder4_16_1_out_18, decoder4_16_1_out_19,
       decoder4_16_1_out_20, decoder_7segments_1_out_5, decoder_7segments_1_out_6, decoder_7segments_1_out_7,
       decoder_7segments_1_out_8, decoder_7segments_1_out_9, decoder_7segments_1_out_10,
       decoder_7segments_1_out_11, decoder_7segments_1_out_12, decoder_7segments_i_1_out_5,
       decoder_7segments_i_1_out_6, decoder_7segments_i_1_out_7, decoder_7segments_i_1_out_8,
       decoder_7segments_i_1_out_9, decoder_7segments_i_1_out_10, decoder_7segments_i_1_out_11, not_1_out,
       not_2_out, not_3_out, not_4_out, not_5_out, not_6_out, not_7_out, transmission_1_p4,
       transmission_2_p4, transmission_3_p4, transmission_4_p4;
  wire [1:0] counter_1_q;
  wire [3:0] counter_3_q, counter_5_q;
  wire [7:0] counter_2_q, counter_4_q;

  Clock clock_1 (.out(clock_1_out));
  Clock clock_2 (.out(clock_2_out));
  Counter #(.max('h3), .width(2)) counter_1 (
    .up(1'b1), .clk(clock_1_out), .Q(counter_1_q));  // open: clr, load, count, D, carry
  Counter #(.max('h7)) counter_2 (
    .up(1'b1), .count(1'b1), .clk(clock_2_out), .Q(counter_2_q));  // open: clr, load, D, carry
  DECODER2_4 decoder2_4_1 (
    .B(counter_1_q[0]), .in_2(counter_1_q[1]), .out_3(decoder2_4_1_out_3), .out_4(decoder2_4_1_out_4),
    .out_5(decoder2_4_1_out_5), .out_6(decoder2_4_1_out_6));
  LED led_1 (.in(decoder2_4_1_out_3));
  LED led_2 (.in(decoder2_4_1_out_4));
  LED led_3 (.in(decoder2_4_1_out_5));
  LED led_4 (.in(decoder2_4_1_out_6));
  not not_1 (not_1_out, counter_1_q[1]);
  not not_2 (not_2_out, counter_1_q[0]);
  not not_3 (not_3_out, counter_1_q[0]);
  not not_4 (not_4_out, in_3);
  not not_5 (not_5_out, in_3);
  not not_6 (not_6_out, in_3);
  not not_7 (not_7_out, in_3);
  and and_1 (out_4, not_1_out, not_2_out);
  and and_2 (out_5, not_1_out, counter_1_q[0]);
  and and_3 (out_6, counter_1_q[1], not_3_out);
  and and_4 (out_7, counter_1_q[1], counter_1_q[0]);
  // Transmission_Gate transmission_1: pin names not known; wires that end beside it: in_1, not_4_out, in_3, transmission_1_p4
  // Transmission_Gate transmission_2: pin names not known; wires that end beside it: in_2, not_5_out, in_3, transmission_2_p4
  // Transmission_Gate transmission_3: pin names not known; wires that end beside it: in_1, not_6_out, in_3, transmission_3_p4
  // Transmission_Gate transmission_4: pin names not known; wires that end beside it: in_2, not_7_out, in_3, transmission_4_p4
  DECODER2_4 decoder2_4_2 (
    .B(transmission_1_p4), .in_2(transmission_2_p4), .out_3(decoder2_4_2_out_3), .out_4(decoder2_4_2_out_4),
    .out_5(decoder2_4_2_out_5), .out_6(decoder2_4_2_out_6));
  DECODER2_4 decoder2_4_3 (
    .B(transmission_3_p4), .in_2(transmission_4_p4), .out_3(decoder2_4_3_out_3), .out_4(decoder2_4_3_out_4),
    .out_5(decoder2_4_3_out_5), .out_6(decoder2_4_3_out_6));
  Counter #(.max('hf), .width(4)) counter_3 (
    .up(1'b1), .clk(clock_3_out), .Q(counter_3_q));  // open: clr, load, count, D, carry
  Clock clock_3 (.out(clock_3_out));
  LED led_5 (.in(decoder2_4_2_out_3));
  LED led_6 (.in(decoder2_4_2_out_4));
  LED led_7 (.in(decoder2_4_2_out_5));
  LED led_8 (.in(decoder2_4_2_out_6));
  LED led_9 (.in(decoder2_4_3_out_3));
  LED led_10 (.in(decoder2_4_3_out_4));
  LED led_11 (.in(decoder2_4_3_out_5));
  LED led_12 (.in(decoder2_4_3_out_6));
  Counter counter_4 (.up(1'b1), .clk(clock_4_out), .Q(counter_4_q));  // open: clr, load, count, D, carry
  Clock clock_4 (.out(clock_4_out));
  Counter #(.max('hf), .width(4)) counter_5 (
    .up(1'b1), .clk(clock_5_out), .Q(counter_5_q));  // open: clr, load, count, D, carry
  Clock clock_5 (.out(clock_5_out));
  decoder_7segments decoder_7segments_1 (
    .in_1(counter_3_q[0]), .in_2(counter_3_q[1]), .in_3(counter_3_q[2]), .in_4(counter_3_q[3]),
    .out_5(decoder_7segments_1_out_5), .out_6(decoder_7segments_1_out_6), .out_7(decoder_7segments_1_out_7),
    .out_8(decoder_7segments_1_out_8), .out_9(decoder_7segments_1_out_9),
    .out_10(decoder_7segments_1_out_10), .out_11(decoder_7segments_1_out_11),
    .out_12(decoder_7segments_1_out_12));
  LED led_13 (.in(decoder4_16_1_out_5));
  decoder4_16 decoder4_16_1 (
    .in_1(counter_4_q[0]), .in_2(counter_4_q[1]), .in_3(counter_4_q[2]), .in_4(counter_4_q[3]),
    .out_5(decoder4_16_1_out_5), .out_6(decoder4_16_1_out_6), .out_7(decoder4_16_1_out_7),
    .out_8(decoder4_16_1_out_8), .out_9(decoder4_16_1_out_9), .out_10(decoder4_16_1_out_10),
    .out_11(decoder4_16_1_out_11), .out_12(decoder4_16_1_out_12), .out_13(decoder4_16_1_out_13),
    .out_14(decoder4_16_1_out_14), .out_15(decoder4_16_1_out_15), .out_16(decoder4_16_1_out_16),
    .out_17(decoder4_16_1_out_17), .out_18(decoder4_16_1_out_18), .out_19(decoder4_16_1_out_19),
    .out_20(decoder4_16_1_out_20));
  LED led_14 (.in(decoder4_16_1_out_6));
  LED led_15 (.in(decoder4_16_1_out_7));
  LED led_16 (.in(decoder4_16_1_out_8));
  LED led_17 (.in(decoder4_16_1_out_9));
  LED led_18 (.in(decoder4_16_1_out_10));
  LED led_19 (.in(decoder4_16_1_out_11));
  LED led_20 (.in(decoder4_16_1_out_12));
  LED led_21 (.in(decoder4_16_1_out_13));
  LED led_22 (.in(decoder4_16_1_out_14));
  LED led_23 (.in(decoder4_16_1_out_15));
  LED led_24 (.in(decoder4_16_1_out_16));
  LED led_25 (.in(decoder4_16_1_out_17));
  LED led_26 (.in(decoder4_16_1_out_18));
  LED led_27 (.in(decoder4_16_1_out_19));
  LED led_28 (.in(decoder4_16_1_out_20));
  decoder_7segments_i decoder_7segments_i_1 (
    .in_1(counter_5_q[0]), .in_2(counter_5_q[1]), .in_3(counter_5_q[2]), .in_4(counter_5_q[3]),
    .out_5(decoder_7segments_i_1_out_5), .out_6(decoder_7segments_i_1_out_6),
    .out_7(decoder_7segments_i_1_out_7), .out_8(decoder_7segments_i_1_out_8),
    .out_9(decoder_7segments_i_1_out_9), .out_10(decoder_7segments_i_1_out_10),
    .out_11(decoder_7segments_i_1_out_11));
  _7_Segment_Display u_7_segment_display_1 (
    .g(decoder_7segments_1_out_5), .f(decoder_7segments_1_out_6), .a(decoder_7segments_1_out_7),
    .b(decoder_7segments_1_out_8), .e(decoder_7segments_1_out_12), .d(decoder_7segments_1_out_11),
    .c(decoder_7segments_1_out_10), .dp(decoder_7segments_1_out_9));
  _7_Segment_Display u_7_segment_display_2 (
    .g(decoder_7segments_i_1_out_5), .f(decoder_7segments_i_1_out_6), .a(decoder_7segments_i_1_out_7),
    .b(decoder_7segments_i_1_out_8), .e(decoder_7segments_i_1_out_9), .d(decoder_7segments_i_1_out_10),
    .c(decoder_7segments_i_1_out_11));  // open: dp

  // Notes on the sheet:
  //   2-4deocder
  //   3-8decoder
  //   A
  //   B
endmodule

module decoder_16_4_hexdisplay (
);

  wire decoder_7segments_i_1_out_5, decoder_7segments_i_1_out_6, decoder_7segments_i_1_out_7,
       decoder_7segments_i_1_out_8, decoder_7segments_i_1_out_9, decoder_7segments_i_1_out_10,
       decoder_7segments_i_1_out_11, decoder_7segments_i_2_out_5, decoder_7segments_i_2_out_6,
       decoder_7segments_i_2_out_7, decoder_7segments_i_2_out_8, decoder_7segments_i_2_out_9,
       decoder_7segments_i_2_out_10, decoder_7segments_i_2_out_11, decoder_7segments_i_3_out_5,
       decoder_7segments_i_3_out_6, decoder_7segments_i_3_out_7, decoder_7segments_i_3_out_8,
       decoder_7segments_i_3_out_9, decoder_7segments_i_3_out_10, decoder_7segments_i_3_out_11,
       decoder_7segments_i_4_out_5, decoder_7segments_i_4_out_6, decoder_7segments_i_4_out_7,
       decoder_7segments_i_4_out_8, decoder_7segments_i_4_out_9, decoder_7segments_i_4_out_10,
       decoder_7segments_i_4_out_11, dipswitch_1_sw1, dipswitch_1_sw2, dipswitch_1_sw3, dipswitch_1_sw4,
       dipswitch_1_sw5, dipswitch_1_sw6, dipswitch_1_sw7, dipswitch_1_sw8, dipswitch_2_sw1, dipswitch_2_sw2,
       dipswitch_2_sw3, dipswitch_2_sw4, dipswitch_2_sw5, dipswitch_2_sw6, dipswitch_2_sw7, dipswitch_2_sw8;

  DipSwitch dipswitch_1 (
    .sw1(dipswitch_1_sw1), .sw2(dipswitch_1_sw2), .sw3(dipswitch_1_sw3), .sw4(dipswitch_1_sw4),
    .sw5(dipswitch_1_sw5), .sw6(dipswitch_1_sw6), .sw7(dipswitch_1_sw7), .sw8(dipswitch_1_sw8));
  DipSwitch dipswitch_2 (
    .sw1(dipswitch_2_sw1), .sw2(dipswitch_2_sw2), .sw3(dipswitch_2_sw3), .sw4(dipswitch_2_sw4),
    .sw5(dipswitch_2_sw5), .sw6(dipswitch_2_sw6), .sw7(dipswitch_2_sw7), .sw8(dipswitch_2_sw8));
  decoder_7segments_i decoder_7segments_i_1 (
    .in_1(dipswitch_1_sw1), .in_2(dipswitch_1_sw2), .in_3(dipswitch_1_sw3), .in_4(dipswitch_1_sw4),
    .out_5(decoder_7segments_i_1_out_5), .out_6(decoder_7segments_i_1_out_6),
    .out_7(decoder_7segments_i_1_out_7), .out_8(decoder_7segments_i_1_out_8),
    .out_9(decoder_7segments_i_1_out_9), .out_10(decoder_7segments_i_1_out_10),
    .out_11(decoder_7segments_i_1_out_11));
  decoder_7segments_i decoder_7segments_i_2 (
    .in_1(dipswitch_1_sw5), .in_2(dipswitch_1_sw6), .in_3(dipswitch_1_sw7), .in_4(dipswitch_1_sw8),
    .out_5(decoder_7segments_i_2_out_5), .out_6(decoder_7segments_i_2_out_6),
    .out_7(decoder_7segments_i_2_out_7), .out_8(decoder_7segments_i_2_out_8),
    .out_9(decoder_7segments_i_2_out_9), .out_10(decoder_7segments_i_2_out_10),
    .out_11(decoder_7segments_i_2_out_11));
  decoder_7segments_i decoder_7segments_i_3 (
    .in_1(dipswitch_2_sw1), .in_2(dipswitch_2_sw2), .in_3(dipswitch_2_sw3), .in_4(dipswitch_2_sw4),
    .out_5(decoder_7segments_i_3_out_5), .out_6(decoder_7segments_i_3_out_6),
    .out_7(decoder_7segments_i_3_out_7), .out_8(decoder_7segments_i_3_out_8),
    .out_9(decoder_7segments_i_3_out_9), .out_10(decoder_7segments_i_3_out_10),
    .out_11(decoder_7segments_i_3_out_11));
  decoder_7segments_i decoder_7segments_i_4 (
    .in_1(dipswitch_2_sw5), .in_2(dipswitch_2_sw6), .in_3(dipswitch_2_sw7), .in_4(dipswitch_2_sw8),
    .out_5(decoder_7segments_i_4_out_5), .out_6(decoder_7segments_i_4_out_6),
    .out_7(decoder_7segments_i_4_out_7), .out_8(decoder_7segments_i_4_out_8),
    .out_9(decoder_7segments_i_4_out_9), .out_10(decoder_7segments_i_4_out_10),
    .out_11(decoder_7segments_i_4_out_11));
  _7_Segment_Display u_7_segment_display_1 (
    .g(decoder_7segments_i_1_out_5), .f(decoder_7segments_i_1_out_6), .a(decoder_7segments_i_1_out_7),
    .b(decoder_7segments_i_1_out_8), .e(decoder_7segments_i_1_out_9), .d(decoder_7segments_i_1_out_10),
    .c(decoder_7segments_i_1_out_11));  // open: dp
  _7_Segment_Display u_7_segment_display_2 (
    .g(decoder_7segments_i_2_out_5), .f(decoder_7segments_i_2_out_6), .a(decoder_7segments_i_2_out_7),
    .b(decoder_7segments_i_2_out_8), .e(decoder_7segments_i_2_out_9), .d(decoder_7segments_i_2_out_10),
    .c(decoder_7segments_i_2_out_11));  // open: dp
  _7_Segment_Display u_7_segment_display_3 (
    .g(decoder_7segments_i_3_out_5), .f(decoder_7segments_i_3_out_6), .a(decoder_7segments_i_3_out_7),
    .b(decoder_7segments_i_3_out_8), .e(decoder_7segments_i_3_out_9), .d(decoder_7segments_i_3_out_10),
    .c(decoder_7segments_i_3_out_11));  // open: dp
  _7_Segment_Display u_7_segment_display_4 (
    .g(decoder_7segments_i_4_out_5), .f(decoder_7segments_i_4_out_6), .a(decoder_7segments_i_4_out_7),
    .b(decoder_7segments_i_4_out_8), .e(decoder_7segments_i_4_out_9), .d(decoder_7segments_i_4_out_10),
    .c(decoder_7segments_i_4_out_11));  // open: dp
endmodule

module display7segment_variablenatation_4 (
);

  wire button_1_out, button_2_out, button_3_out, button_4_out, button_5_out, button_6_out, button_7_out,
       button_8_out, decoder_7segments_2_out_5, decoder_7segments_2_out_6, decoder_7segments_2_out_7,
       decoder_7segments_2_out_8, decoder_7segments_2_out_9, decoder_7segments_2_out_10,
       decoder_7segments_2_out_11, decoder_7segments_2_out_12, decoder_7segments_i_1_out_5,
       decoder_7segments_i_1_out_6, decoder_7segments_i_1_out_7, decoder_7segments_i_1_out_8,
       decoder_7segments_i_1_out_9, decoder_7segments_i_1_out_10, decoder_7segments_i_1_out_11,
       decoder_7segments_i_2_out_5, decoder_7segments_i_2_out_6, decoder_7segments_i_2_out_7,
       decoder_7segments_i_2_out_8, decoder_7segments_i_2_out_9, decoder_7segments_i_2_out_10,
       decoder_7segments_i_2_out_11, dipswitch_1_sw1, dipswitch_1_sw2, dipswitch_1_sw3, dipswitch_1_sw4,
       dipswitch_1_sw8, dipswitch_2_sw1, dipswitch_2_sw2, dipswitch_2_sw3, dipswitch_2_sw4, dipswitch_2_sw8,
       not_1_out, not_2_out, not_3_out, not_4_out, transmission_1_p4, transmission_2_p4, transmission_3_p4,
       transmission_4_p4, transmission_5_p4, transmission_6_p4, transmission_7_p4, transmission_8_p4,
       transmission_9_p4, transmission_10_p4, transmission_11_p4, transmission_12_p4, transmission_13_p4,
       transmission_14_p4, transmission_15_p4, transmission_20_p4;

  DipSwitch dipswitch_1 (
    .sw1(dipswitch_1_sw1), .sw2(dipswitch_1_sw2), .sw3(dipswitch_1_sw3), .sw4(dipswitch_1_sw4),
    .sw8(dipswitch_1_sw8));  // open: sw5, sw6, sw7
  not not_1 (not_1_out, dipswitch_1_sw8);
  not not_2 (not_2_out, dipswitch_1_sw8);
  // Transmission_Gate transmission_1: pin names not known; wires that end beside it: dipswitch_1_sw1, not_1_out, dipswitch_1_sw8, transmission_1_p4
  // Transmission_Gate transmission_2: pin names not known; wires that end beside it: dipswitch_1_sw2, not_1_out, dipswitch_1_sw8, transmission_2_p4
  // Transmission_Gate transmission_3: pin names not known; wires that end beside it: dipswitch_1_sw3, not_1_out, dipswitch_1_sw8, transmission_3_p4
  // Transmission_Gate transmission_4: pin names not known; wires that end beside it: dipswitch_1_sw4, not_1_out, dipswitch_1_sw8, transmission_4_p4
  // Transmission_Gate transmission_5: pin names not known; wires that end beside it: dipswitch_1_sw1, dipswitch_1_sw8, not_2_out, transmission_5_p4
  // Transmission_Gate transmission_6: pin names not known; wires that end beside it: dipswitch_1_sw2, dipswitch_1_sw8, not_2_out, transmission_6_p4
  // Transmission_Gate transmission_7: pin names not known; wires that end beside it: dipswitch_1_sw3, dipswitch_1_sw8, not_2_out, transmission_7_p4
  // Transmission_Gate transmission_8: pin names not known; wires that end beside it: dipswitch_1_sw4, dipswitch_1_sw8, not_2_out, transmission_8_p4
  decoder_7segments_i decoder_7segments_i_1 (
    .in_1(transmission_1_p4), .in_2(transmission_2_p4), .in_3(transmission_3_p4), .in_4(transmission_4_p4),
    .out_5(decoder_7segments_i_1_out_5), .out_6(decoder_7segments_i_1_out_6),
    .out_7(decoder_7segments_i_1_out_7), .out_8(decoder_7segments_i_1_out_8),
    .out_9(decoder_7segments_i_1_out_9), .out_10(decoder_7segments_i_1_out_10),
    .out_11(decoder_7segments_i_1_out_11));
  decoder_7segments decoder_7segments_1 (
    .in_1(transmission_5_p4), .in_2(transmission_6_p4), .in_3(transmission_7_p4), .in_4(transmission_8_p4));  // open: out_5, out_6, out_7, out_8, out_9, out_10, out_11, out_12
  DipSwitch dipswitch_2 (
    .sw1(dipswitch_2_sw1), .sw2(dipswitch_2_sw2), .sw3(dipswitch_2_sw3), .sw4(dipswitch_2_sw4),
    .sw8(dipswitch_2_sw8));  // open: sw5, sw6, sw7
  _7_Segment_Display u_7_segment_display_1 (
    .g(decoder_7segments_i_1_out_5), .f(decoder_7segments_i_1_out_6), .a(decoder_7segments_i_1_out_7),
    .b(decoder_7segments_i_1_out_8), .e(decoder_7segments_i_1_out_9), .d(decoder_7segments_i_1_out_10),
    .c(decoder_7segments_i_1_out_11));  // open: dp
  decoder_7segments_i decoder_7segments_i_2 (
    .in_1(dipswitch_2_sw1), .in_2(dipswitch_2_sw2), .in_3(dipswitch_2_sw3), .in_4(dipswitch_2_sw4),
    .out_5(decoder_7segments_i_2_out_5), .out_6(decoder_7segments_i_2_out_6),
    .out_7(decoder_7segments_i_2_out_7), .out_8(decoder_7segments_i_2_out_8),
    .out_9(decoder_7segments_i_2_out_9), .out_10(decoder_7segments_i_2_out_10),
    .out_11(decoder_7segments_i_2_out_11));
  decoder_7segments decoder_7segments_2 (
    .in_1(dipswitch_2_sw1), .in_2(dipswitch_2_sw2), .in_3(dipswitch_2_sw3), .in_4(dipswitch_2_sw4),
    .out_5(decoder_7segments_2_out_5), .out_6(decoder_7segments_2_out_6), .out_7(decoder_7segments_2_out_7),
    .out_8(decoder_7segments_2_out_8), .out_9(decoder_7segments_2_out_9),
    .out_10(decoder_7segments_2_out_10), .out_11(decoder_7segments_2_out_11),
    .out_12(decoder_7segments_2_out_12));
  not not_3 (not_3_out, dipswitch_2_sw8);
  not not_4 (not_4_out, dipswitch_2_sw8);
  // Transmission_Gate transmission_9: pin names not known; wires that end beside it: decoder_7segments_i_2_out_5, not_3_out, dipswitch_2_sw8, transmission_9_p4
  // Transmission_Gate transmission_10: pin names not known; wires that end beside it: decoder_7segments_i_2_out_6, not_3_out, dipswitch_2_sw8, transmission_10_p4
  // Transmission_Gate transmission_11: pin names not known; wires that end beside it: decoder_7segments_i_2_out_7, not_3_out, dipswitch_2_sw8, transmission_11_p4
  // Transmission_Gate transmission_12: pin names not known; wires that end beside it: decoder_7segments_i_2_out_8, not_3_out, dipswitch_2_sw8, transmission_12_p4
  // Transmission_Gate transmission_13: pin names not known; wires that end beside it: decoder_7segments_i_2_out_9, not_3_out, dipswitch_2_sw8, transmission_13_p4
  // Transmission_Gate transmission_14: pin names not known; wires that end beside it: decoder_7segments_i_2_out_10, not_3_out, dipswitch_2_sw8, transmission_14_p4
  // Transmission_Gate transmission_15: pin names not known; wires that end beside it: decoder_7segments_i_2_out_11, not_3_out, dipswitch_2_sw8, transmission_15_p4
  // Transmission_Gate transmission_16: pin names not known; wires that end beside it: decoder_7segments_2_out_5, dipswitch_2_sw8, not_4_out, transmission_9_p4
  // Transmission_Gate transmission_17: pin names not known; wires that end beside it: decoder_7segments_2_out_6, dipswitch_2_sw8, not_4_out, transmission_10_p4
  // Transmission_Gate transmission_18: pin names not known; wires that end beside it: decoder_7segments_2_out_7, dipswitch_2_sw8, not_4_out, transmission_11_p4
  // Transmission_Gate transmission_19: pin names not known; wires that end beside it: decoder_7segments_2_out_8, dipswitch_2_sw8, not_4_out, transmission_12_p4
  // Transmission_Gate transmission_20: pin names not known; wires that end beside it: decoder_7segments_2_out_9, dipswitch_2_sw8, not_4_out, transmission_20_p4
  // Transmission_Gate transmission_21: pin names not known; wires that end beside it: decoder_7segments_2_out_10, dipswitch_2_sw8, not_4_out, transmission_15_p4
  // Transmission_Gate transmission_22: pin names not known; wires that end beside it: decoder_7segments_2_out_11, dipswitch_2_sw8, not_4_out, transmission_14_p4
  // Transmission_Gate transmission_23: pin names not known; wires that end beside it: decoder_7segments_2_out_12, dipswitch_2_sw8, not_4_out, transmission_13_p4
  _7_Segment_Display u_7_segment_display_2 (
    .g(transmission_9_p4), .f(transmission_10_p4), .a(transmission_11_p4), .b(transmission_12_p4),
    .e(transmission_13_p4), .d(transmission_14_p4), .c(transmission_15_p4), .dp(transmission_20_p4));
  Button button_1 (.out(button_1_out));
  Button button_2 (.out(button_2_out));
  Button button_3 (.out(button_3_out));
  Button button_4 (.out(button_4_out));
  _7_Segment_Display u_7_segment_display_3 (
    .g(button_4_out), .f(button_3_out), .a(button_2_out), .b(button_1_out), .e(button_5_out),
    .d(button_6_out), .c(button_7_out), .dp(button_8_out));
  Button button_5 (.out(button_5_out));
  Button button_6 (.out(button_6_out));
  Button button_7 (.out(button_7_out));
  Button button_8 (.out(button_8_out));
endmodule

module subadder_4bits (
);

  wire decoder_7segments_i_1_out_5, decoder_7segments_i_1_out_6, decoder_7segments_i_1_out_7,
       decoder_7segments_i_1_out_8, decoder_7segments_i_1_out_9, decoder_7segments_i_1_out_10,
       decoder_7segments_i_1_out_11, decoder_7segments_i_2_out_5, decoder_7segments_i_2_out_6,
       decoder_7segments_i_2_out_7, decoder_7segments_i_2_out_8, decoder_7segments_i_2_out_9,
       decoder_7segments_i_2_out_10, decoder_7segments_i_2_out_11, decoder_7segments_i_3_out_5,
       decoder_7segments_i_3_out_6, decoder_7segments_i_3_out_7, decoder_7segments_i_3_out_8,
       decoder_7segments_i_3_out_9, decoder_7segments_i_3_out_10, decoder_7segments_i_3_out_11,
       dipswitch_1_sw1, dipswitch_1_sw2, dipswitch_1_sw3, dipswitch_1_sw4, dipswitch_2_sw1, dipswitch_2_sw2,
       dipswitch_2_sw3, dipswitch_2_sw4, fullsubber_1_out_4, fullsubber_1_out_5, fullsubber_2_out_4,
       fullsubber_2_out_5, fullsubber_3_out_4, fullsubber_3_out_5, fullsubber_4_out_4, fullsubber_4_out_5;

  DipSwitch dipswitch_1 (
    .sw1(dipswitch_1_sw1), .sw2(dipswitch_1_sw2), .sw3(dipswitch_1_sw3), .sw4(dipswitch_1_sw4));  // open: sw5, sw6, sw7, sw8
  DipSwitch dipswitch_2 (
    .sw1(dipswitch_2_sw1), .sw2(dipswitch_2_sw2), .sw3(dipswitch_2_sw3), .sw4(dipswitch_2_sw4));  // open: sw5, sw6, sw7, sw8
  decoder_7segments_i decoder_7segments_i_1 (
    .in_1(dipswitch_1_sw1), .in_2(dipswitch_1_sw2), .in_3(dipswitch_1_sw3), .in_4(dipswitch_1_sw4),
    .out_5(decoder_7segments_i_1_out_5), .out_6(decoder_7segments_i_1_out_6),
    .out_7(decoder_7segments_i_1_out_7), .out_8(decoder_7segments_i_1_out_8),
    .out_9(decoder_7segments_i_1_out_9), .out_10(decoder_7segments_i_1_out_10),
    .out_11(decoder_7segments_i_1_out_11));
  decoder_7segments_i decoder_7segments_i_2 (
    .in_1(dipswitch_2_sw1), .in_2(dipswitch_2_sw2), .in_3(dipswitch_2_sw3), .in_4(dipswitch_2_sw4),
    .out_5(decoder_7segments_i_2_out_5), .out_6(decoder_7segments_i_2_out_6),
    .out_7(decoder_7segments_i_2_out_7), .out_8(decoder_7segments_i_2_out_8),
    .out_9(decoder_7segments_i_2_out_9), .out_10(decoder_7segments_i_2_out_10),
    .out_11(decoder_7segments_i_2_out_11));
  _7_Segment_Display u_7_segment_display_1 (
    .g(decoder_7segments_i_1_out_5), .f(decoder_7segments_i_1_out_6), .a(decoder_7segments_i_1_out_7),
    .b(decoder_7segments_i_1_out_8), .e(decoder_7segments_i_1_out_9), .d(decoder_7segments_i_1_out_10),
    .c(decoder_7segments_i_1_out_11));  // open: dp
  _7_Segment_Display u_7_segment_display_2 (
    .g(decoder_7segments_i_2_out_5), .f(decoder_7segments_i_2_out_6), .a(decoder_7segments_i_2_out_7),
    .b(decoder_7segments_i_2_out_8), .e(decoder_7segments_i_2_out_9), .d(decoder_7segments_i_2_out_10),
    .c(decoder_7segments_i_2_out_11));  // open: dp
  fullsubber fullsubber_1 (
    .in_1(dipswitch_1_sw1), .in_2(dipswitch_2_sw1), .in_3(1'b0), .out_4(fullsubber_1_out_4),
    .out_5(fullsubber_1_out_5));
  fullsubber fullsubber_2 (
    .in_1(dipswitch_1_sw2), .in_2(dipswitch_2_sw2), .in_3(fullsubber_1_out_5), .out_4(fullsubber_2_out_4),
    .out_5(fullsubber_2_out_5));
  fullsubber fullsubber_3 (
    .in_1(dipswitch_1_sw3), .in_2(dipswitch_2_sw3), .in_3(fullsubber_2_out_5), .out_4(fullsubber_3_out_4),
    .out_5(fullsubber_3_out_5));
  fullsubber fullsubber_4 (
    .in_1(dipswitch_1_sw4), .in_2(dipswitch_2_sw4), .in_3(fullsubber_3_out_5), .out_4(fullsubber_4_out_4),
    .out_5(fullsubber_4_out_5));
  decoder_7segments_i decoder_7segments_i_3 (
    .in_1(fullsubber_1_out_4), .in_2(fullsubber_2_out_4), .in_3(fullsubber_3_out_4),
    .in_4(fullsubber_4_out_4), .out_5(decoder_7segments_i_3_out_5), .out_6(decoder_7segments_i_3_out_6),
    .out_7(decoder_7segments_i_3_out_7), .out_8(decoder_7segments_i_3_out_8),
    .out_9(decoder_7segments_i_3_out_9), .out_10(decoder_7segments_i_3_out_10),
    .out_11(decoder_7segments_i_3_out_11));
  _7_Segment_Display u_7_segment_display_3 (
    .g(decoder_7segments_i_3_out_5), .f(decoder_7segments_i_3_out_6), .a(decoder_7segments_i_3_out_7),
    .b(decoder_7segments_i_3_out_8), .e(decoder_7segments_i_3_out_9), .d(decoder_7segments_i_3_out_10),
    .c(decoder_7segments_i_3_out_11));  // open: dp
  LED led_1 (.in(fullsubber_4_out_5));
endmodule

module fulladder_subadder (
  input  in_1,
  input  in_2,
  input  in_3,
  input  in_4,
  input  in_5,
  input  in_6,
  input  in_7,
  output out_8,
  output out_9,
  output out_10,
  output OutCarry
);

  wire and_1_out, and_2_out, xor_1_out, xor_2_out;

  xor xor_1 (xor_1_out, in_5, in_6);
  and and_1 (and_1_out, in_6, in_5);
  xor xor_2 (xor_2_out, in_2, in_3);
  and and_2 (and_2_out, xor_1_out, in_7);
  xor xor_3 (out_10, xor_1_out, in_7);
  or or_1 (OutCarry, and_1_out, and_2_out);
  xor xor_4 (out_8, xor_2_out, in_4);

  // Notes on the sheet:
  //   A
  //   B
  //   A
  //   B
  //   Sum
  //   Sum
endmodule

module halfsubber (
  input  in_1,
  input  in_2,
  output out_3,
  output out_4
);

  xor xor_1 (out_3, in_1, in_2);
  and and_1 (out_4, out_3, in_2);

  // Notes on the sheet:
  //   A
  //   B
endmodule

module fullsubber (
  input  in_1,
  input  in_2,
  input  in_3,
  output out_4,
  output out_5
);

  wire halfsubber_1_out_3, halfsubber_1_out_4, halfsubber_2_out_4;

  halfsubber halfsubber_1 (.in_1(in_1), .in_2(in_2), .out_3(halfsubber_1_out_3), .out_4(halfsubber_1_out_4));
  halfsubber halfsubber_2 (.in_1(halfsubber_1_out_3), .in_2(in_3), .out_3(out_4), .out_4(halfsubber_2_out_4));
  or or_1 (out_5, halfsubber_1_out_4, halfsubber_2_out_4);
endmodule

module subadder_4bits_signandmagnitude (
  input  in_1,
  input  in_2,
  input  in_3,
  input  in_4,
  input  in_5,
  input  in_6,
  input  in_7,
  input  in_8,
  output out_9,
  output out_10,
  output out_11,
  output out_12,
  output out_13
);

  wire and_1_out, and_2_out, cmp_3bits_1_out_7, decoder_7segments_i_1_out_5, decoder_7segments_i_1_out_6,
       decoder_7segments_i_1_out_7, decoder_7segments_i_1_out_8, decoder_7segments_i_1_out_9,
       decoder_7segments_i_1_out_10, decoder_7segments_i_1_out_11, decoder_7segments_i_2_out_5,
       decoder_7segments_i_2_out_6, decoder_7segments_i_2_out_7, decoder_7segments_i_2_out_8,
       decoder_7segments_i_2_out_9, decoder_7segments_i_2_out_10, decoder_7segments_i_2_out_11,
       decoder_7segments_i_3_out_5, decoder_7segments_i_3_out_6, decoder_7segments_i_3_out_7,
       decoder_7segments_i_3_out_8, decoder_7segments_i_3_out_9, decoder_7segments_i_3_out_10,
       decoder_7segments_i_3_out_11, fulladder_1_out_4, fulladder_1_outcarry, fulladder_2_out_4,
       fulladder_2_outcarry, fulladder_3_out_4, fulladder_3_outcarry, fullsubber_1_out_4, fullsubber_1_out_5,
       fullsubber_2_out_4, fullsubber_2_out_5, fullsubber_3_out_4, fullsubber_3_out_5, mux2_1_out_4,
       mux2_2_out_4, mux2_3_out_4, mux2_4_out_4, mux2_5_out_4, mux2_6_out_4, xor_1_out;

  decoder_7segments_i decoder_7segments_i_1 (
    .in_1(in_2), .in_2(in_3), .in_3(in_4), .in_4(1'b0), .out_5(decoder_7segments_i_1_out_5),
    .out_6(decoder_7segments_i_1_out_6), .out_7(decoder_7segments_i_1_out_7),
    .out_8(decoder_7segments_i_1_out_8), .out_9(decoder_7segments_i_1_out_9),
    .out_10(decoder_7segments_i_1_out_10), .out_11(decoder_7segments_i_1_out_11));
  decoder_7segments_i decoder_7segments_i_2 (
    .in_1(in_6), .in_2(in_7), .in_3(in_8), .in_4(1'b0), .out_5(decoder_7segments_i_2_out_5),
    .out_6(decoder_7segments_i_2_out_6), .out_7(decoder_7segments_i_2_out_7),
    .out_8(decoder_7segments_i_2_out_8), .out_9(decoder_7segments_i_2_out_9),
    .out_10(decoder_7segments_i_2_out_10), .out_11(decoder_7segments_i_2_out_11));
  _7_Segment_Display u_7_segment_display_1 (
    .g(decoder_7segments_i_1_out_5), .f(decoder_7segments_i_1_out_6), .a(decoder_7segments_i_1_out_7),
    .b(decoder_7segments_i_1_out_8), .e(decoder_7segments_i_1_out_9), .d(decoder_7segments_i_1_out_10),
    .c(decoder_7segments_i_1_out_11));  // open: dp
  _7_Segment_Display u_7_segment_display_2 (
    .g(decoder_7segments_i_2_out_5), .f(decoder_7segments_i_2_out_6), .a(decoder_7segments_i_2_out_7),
    .b(decoder_7segments_i_2_out_8), .e(decoder_7segments_i_2_out_9), .d(decoder_7segments_i_2_out_10),
    .c(decoder_7segments_i_2_out_11));  // open: dp
  and and_1 (and_1_out, in_1, in_5);
  xor xor_1 (xor_1_out, in_1, in_5);
  cmp_3bits cmp_3bits_1 (
    .in_1(in_2), .in_2(in_3), .in_3(in_4), .B(in_6), .in_5(in_7), .in_6(in_8), .out_7(cmp_3bits_1_out_7));
  and and_2 (and_2_out, cmp_3bits_1_out_7, xor_1_out);
  MUX2 mux2_1 (.in_2(in_2), .in_3(in_6), .in_1(cmp_3bits_1_out_7), .out_4(mux2_1_out_4));
  MUX2 mux2_2 (.in_2(in_6), .in_3(in_2), .in_1(cmp_3bits_1_out_7), .out_4(mux2_2_out_4));
  MUX2 mux2_3 (.in_2(in_3), .in_3(in_7), .in_1(cmp_3bits_1_out_7), .out_4(mux2_3_out_4));
  MUX2 mux2_4 (.in_2(in_7), .in_3(in_3), .in_1(cmp_3bits_1_out_7), .out_4(mux2_4_out_4));
  MUX2 mux2_5 (.in_2(in_4), .in_3(in_8), .in_1(cmp_3bits_1_out_7), .out_4(mux2_5_out_4));
  MUX2 mux2_6 (.in_2(in_8), .in_3(in_4), .in_1(cmp_3bits_1_out_7), .out_4(mux2_6_out_4));
  or or_1 (out_13, and_1_out, and_2_out);
  fullsubber fullsubber_1 (
    .in_1(mux2_1_out_4), .in_2(mux2_2_out_4), .in_3(1'b0), .out_4(fullsubber_1_out_4),
    .out_5(fullsubber_1_out_5));
  fullsubber fullsubber_2 (
    .in_1(mux2_3_out_4), .in_2(mux2_4_out_4), .in_3(fullsubber_1_out_5), .out_4(fullsubber_2_out_4),
    .out_5(fullsubber_2_out_5));
  fullsubber fullsubber_3 (
    .in_1(mux2_5_out_4), .in_2(mux2_6_out_4), .in_3(fullsubber_2_out_5), .out_4(fullsubber_3_out_4),
    .out_5(fullsubber_3_out_5));
  fulladder fulladder_1 (
    .in_1(in_2), .in_2(in_6), .in_3(1'b0), .out_4(fulladder_1_out_4), .OutCarry(fulladder_1_outcarry));
  fulladder fulladder_2 (
    .in_1(in_3), .in_2(in_7), .in_3(fulladder_1_outcarry), .out_4(fulladder_2_out_4),
    .OutCarry(fulladder_2_outcarry));
  fulladder fulladder_3 (
    .in_1(in_4), .in_2(in_8), .in_3(fulladder_2_outcarry), .out_4(fulladder_3_out_4),
    .OutCarry(fulladder_3_outcarry));
  MUX2 mux2_7 (.in_2(fulladder_1_out_4), .in_3(fullsubber_1_out_4), .in_1(xor_1_out), .out_4(out_9));
  MUX2 mux2_8 (.in_2(fulladder_2_out_4), .in_3(fullsubber_2_out_4), .in_1(xor_1_out), .out_4(out_10));
  MUX2 mux2_9 (.in_2(fulladder_3_out_4), .in_3(fullsubber_3_out_4), .in_1(xor_1_out), .out_4(out_11));
  MUX2 mux2_10 (.in_2(fulladder_3_outcarry), .in_3(fullsubber_3_out_5), .in_1(xor_1_out), .out_4(out_12));
  LED led_1 ();  // open: in
  decoder_7segments_i decoder_7segments_i_3 (
    .in_1(out_9), .in_2(out_10), .in_3(out_11), .in_4(out_12), .out_5(decoder_7segments_i_3_out_5),
    .out_6(decoder_7segments_i_3_out_6), .out_7(decoder_7segments_i_3_out_7),
    .out_8(decoder_7segments_i_3_out_8), .out_9(decoder_7segments_i_3_out_9),
    .out_10(decoder_7segments_i_3_out_10), .out_11(decoder_7segments_i_3_out_11));
  _7_Segment_Display u_7_segment_display_3 (
    .g(decoder_7segments_i_3_out_5), .f(decoder_7segments_i_3_out_6), .a(decoder_7segments_i_3_out_7),
    .b(decoder_7segments_i_3_out_8), .e(decoder_7segments_i_3_out_9), .d(decoder_7segments_i_3_out_10),
    .c(decoder_7segments_i_3_out_11));  // open: dp

  // Notes on the sheet:
  //   如果A大于B，那么输出0；如果B大于A，那么输出1；如果相等，输出0
endmodule

module cmp_1bits (
  input  in_1,
  input  in_2,
  output out_3,
  output out_4
);

  wire not_1_out, xor_1_out;

  xor xor_1 (xor_1_out, in_1, in_2);
  not not_1 (not_1_out, in_1);
  and and_1 (out_4, not_1_out, in_2);
  not not_2 (out_3, xor_1_out);
endmodule

module cmp_3bits (
  input  in_1,
  input  in_2,
  input  in_3,
  input  B,
  input  in_5,
  input  in_6,
  output out_7
);

  wire and_1_out, and_2_out, cmp_1bits_1_out_3, cmp_1bits_1_out_4, cmp_1bits_2_out_3, cmp_1bits_2_out_4,
       cmp_1bits_3_out_4;

  cmp_1bits cmp_1bits_1 (.in_1(in_1), .in_2(B), .out_3(cmp_1bits_1_out_3), .out_4(cmp_1bits_1_out_4));
  cmp_1bits cmp_1bits_2 (.in_1(in_2), .in_2(in_5), .out_3(cmp_1bits_2_out_3), .out_4(cmp_1bits_2_out_4));
  cmp_1bits cmp_1bits_3 (.in_1(in_3), .in_2(in_6), .out_4(cmp_1bits_3_out_4));  // open: out_3
  and and_1 (and_1_out, cmp_1bits_2_out_4, cmp_1bits_1_out_3);
  and and_2 (and_2_out, cmp_1bits_3_out_4, cmp_1bits_1_out_3, cmp_1bits_2_out_3);
  or or_1 (out_7, cmp_1bits_1_out_4, and_1_out, and_2_out);

  // Notes on the sheet:
  //   A
  //   如果A大于B，那么输出00；如果B大于A，那么输出10；如果相等，输出01
  //   如果A大于B，那么输出0；如果B大于A，那么输出1；如果相等，输出0(需要独热码么?)
endmodule

module PrimeCounter4_2 (
  input  in_1,
  input  in_2,
  input  in_3,
  input  in_4,
  output out_5,
  output out_6
);

  wire and_1_out, and_2_out, not_1_out;

  or or_1 (out_5, in_3, in_4);
  not not_1 (not_1_out, out_5);
  and and_1 (and_1_out, in_2, not_1_out);
  and and_2 (and_2_out, in_4, out_5);
  or or_2 (out_6, and_1_out, and_2_out);
endmodule

module MUX2 (
  input  in_1,
  input  in_2,
  input  in_3,
  output out_4
);

  wire not_1_out;

  not not_1 (not_1_out, in_1);
  // Transmission_Gate transmission_1: pin names not known; wires that end beside it: in_2, in_1, not_1_out, out_4
  // Transmission_Gate transmission_2: pin names not known; wires that end beside it: in_3, not_1_out, in_1, out_4
endmodule

module subadder_4bits_onescomplement (
  output out_1
);

  wire decoder_7segments_i_1_out_5, decoder_7segments_i_1_out_6, decoder_7segments_i_1_out_7,
       decoder_7segments_i_1_out_8, decoder_7segments_i_1_out_9, decoder_7segments_i_1_out_10,
       decoder_7segments_i_1_out_11, decoder_onescomplement_megnitude_1_out_5,
       decoder_onescomplement_megnitude_1_out_6, decoder_onescomplement_megnitude_1_out_7,
       decoder_onescomplement_megnitude_1_out_8, decoder_onescomplement_megnitude_2_out_5,
       decoder_onescomplement_megnitude_2_out_6, decoder_onescomplement_megnitude_2_out_7,
       decoder_onescomplement_megnitude_2_out_8, dipswitch_1_sw1, dipswitch_1_sw2, dipswitch_1_sw3,
       dipswitch_1_sw4, dipswitch_2_sw1, dipswitch_2_sw2, dipswitch_2_sw3, dipswitch_2_sw4,
       subadder_4bits_signandmagnitude_1_out_9, subadder_4bits_signandmagnitude_1_out_10,
       subadder_4bits_signandmagnitude_1_out_11, subadder_4bits_signandmagnitude_1_out_12;

  DipSwitch dipswitch_1 (
    .sw1(dipswitch_1_sw1), .sw2(dipswitch_1_sw2), .sw3(dipswitch_1_sw3), .sw4(dipswitch_1_sw4));  // open: sw5, sw6, sw7, sw8
  DipSwitch dipswitch_2 (
    .sw1(dipswitch_2_sw1), .sw2(dipswitch_2_sw2), .sw3(dipswitch_2_sw3), .sw4(dipswitch_2_sw4));  // open: sw5, sw6, sw7, sw8
  decoder_onescomplement_megnitude decoder_onescomplement_megnitude_1 (
    .in_1(dipswitch_1_sw1), .in_2(dipswitch_1_sw2), .in_3(dipswitch_1_sw3), .in_4(dipswitch_1_sw4),
    .out_5(decoder_onescomplement_megnitude_1_out_5), .out_6(decoder_onescomplement_megnitude_1_out_6),
    .out_7(decoder_onescomplement_megnitude_1_out_7), .out_8(decoder_onescomplement_megnitude_1_out_8));
  decoder_onescomplement_megnitude decoder_onescomplement_megnitude_2 (
    .in_1(dipswitch_2_sw1), .in_2(dipswitch_2_sw2), .in_3(dipswitch_2_sw3), .in_4(dipswitch_2_sw4),
    .out_5(decoder_onescomplement_megnitude_2_out_5), .out_6(decoder_onescomplement_megnitude_2_out_6),
    .out_7(decoder_onescomplement_megnitude_2_out_7), .out_8(decoder_onescomplement_megnitude_2_out_8));
  subadder_4bits_signandmagnitude subadder_4bits_signandmagnitude_1 (
    .in_1(decoder_onescomplement_megnitude_1_out_5), .in_2(decoder_onescomplement_megnitude_1_out_6),
    .in_3(decoder_onescomplement_megnitude_1_out_7), .in_4(decoder_onescomplement_megnitude_1_out_8),
    .in_5(decoder_onescomplement_megnitude_2_out_5), .in_6(decoder_onescomplement_megnitude_2_out_6),
    .in_7(decoder_onescomplement_megnitude_2_out_7), .in_8(decoder_onescomplement_megnitude_2_out_8),
    .out_9(subadder_4bits_signandmagnitude_1_out_9), .out_10(subadder_4bits_signandmagnitude_1_out_10),
    .out_11(subadder_4bits_signandmagnitude_1_out_11), .out_12(subadder_4bits_signandmagnitude_1_out_12),
    .out_13(out_1));
  decoder_7segments_i decoder_7segments_i_1 (
    .in_1(subadder_4bits_signandmagnitude_1_out_9), .in_2(subadder_4bits_signandmagnitude_1_out_10),
    .in_3(subadder_4bits_signandmagnitude_1_out_11), .in_4(subadder_4bits_signandmagnitude_1_out_12),
    .out_5(decoder_7segments_i_1_out_5), .out_6(decoder_7segments_i_1_out_6),
    .out_7(decoder_7segments_i_1_out_7), .out_8(decoder_7segments_i_1_out_8),
    .out_9(decoder_7segments_i_1_out_9), .out_10(decoder_7segments_i_1_out_10),
    .out_11(decoder_7segments_i_1_out_11));
  _7_Segment_Display u_7_segment_display_1 (
    .g(decoder_7segments_i_1_out_5), .f(decoder_7segments_i_1_out_6), .a(decoder_7segments_i_1_out_7),
    .b(decoder_7segments_i_1_out_8), .e(decoder_7segments_i_1_out_9), .d(decoder_7segments_i_1_out_10),
    .c(decoder_7segments_i_1_out_11));  // open: dp
endmodule

module decoder_onescomplement_megnitude (
  input  in_1,
  input  in_2,
  input  in_3,
  input  in_4,
  output out_5,
  output out_6,
  output out_7,
  output out_8
);

  MUX_not mux_not_1 (.in_2(in_2), .in_1(in_1), .out_3(out_6));
  MUX_not mux_not_2 (.in_2(in_3), .in_1(in_1), .out_3(out_7));
  MUX_not mux_not_3 (.in_2(in_4), .in_1(in_1), .out_3(out_8));

  assign out_5 = in_1;
endmodule

module MUX_not (
  input  in_1,
  input  in_2,
  output out_3
);

  xor xor_1 (out_3, in_1, in_2);
endmodule
