// Logisim project PrimeCounter.circ as structural Verilog: 9 circuits, main circuit main
module main (
  input  in_1,
  input  in_2,
  input  in_3,
  input  in_4,
  input  in_5,
  input  in_6,
  input  in_7,
  input  in_8,
  input  in_9,
  input  in_10,
  input  in_11,
  input  in_12,
  input  in_13,
  input  in_14,
  output out_15,
  output out_16,
  output out_17
);

  wire clock_1_out, primecounter4_2_1_out_5, primecounter4_2_1_out_6;
  wire [3:0] counter_1_q;

  Counter #(.max('hf), .width(4)) counter_1 (
    .up(1'b1), .clk(clock_1_out), .Q(counter_1_q));  // open: clr, load, count, D, carry
  Clock clock_1 (.out(clock_1_out));
  sel21 sel21_1 ();  // open: in_2, in_3, in_1, out_4
  LED led_1 (.in(primecounter4_2_1_out_5));
  PrimeCounter4_2 primecounter4_2_1 (
    .in_1(counter_1_q[0]), .in_2(counter_1_q[1]), .in_3(counter_1_q[2]), .in_4(counter_1_q[3]),
    .out_5(primecounter4_2_1_out_5), .out_6(primecounter4_2_1_out_6));
  LED led_2 (.in(primecounter4_2_1_out_6));
  // sel_3bits_4_1 sel_3bits_4_1_1: pin names not known; wires that end beside it: in_3, in_4, in_5, in_6, in_7, in_8, in_9, in_10, in_11, in_12, in_13, in_14, in_1, in_2, out_15, out_16, out_17
endmodule

module PrimeCounter4_2 (
  input  in_1,
  input  in_2,
  input  in_3,
  input  in_4,
  output out_5,
  output out_6
);

  wire and_1_out, and_2_out, not_1_out;

  or or_1 (out_5, in_3, in_4);
  not not_1 (not_1_out, out_5);
  and and_1 (and_1_out, in_2, not_1_out);
  and and_2 (and_2_out, in_4, out_5);
  or or_2 (out_6, and_1_out, and_2_out);
endmodule

module XOR3bits (
  input  in_1,
  input  in_2,
  input  in_3
);
endmodule

module Counter4_2 (
  input  in_1,
  input  in_2,
  input  in_3,
  input  in_4,
  output out_5,
  output out_6
);

  or or_1 (out_5, in_2, in_4);
  or or_2 (out_6, in_3, in_4);
endmodule

module sel21 (
  input  in_1,
  input  in_2,
  input  in_3,
  output out_4
);

  wire not_1_out;

  not not_1 (not_1_out, in_1);
  // Transmission_Gate transmission_1: pin names not known; wires that end beside it: in_2, in_1, not_1_out, out_4
  // Transmission_Gate transmission_2: pin names not known; wires that end beside it: in_3, not_1_out, in_1, out_4
endmodule

module sel_3bits_4_1 (
  input  in_1,
  input  in_2,
  input  in_3,
  input  in_4,
  input  in_5,
  input  in_6,
  input  in_7,
  input  in_8,
  input  in_9,
  input  in_10,
  input  in_11,
  input  in_12,
  input  in_13,
  input  in_14,
  output out_15,
  output out_16,
  output out_17
);

  wire transmission_1_p2, transmission_1_p3, transmission_4_p2, transmission_4_p3, transmission_7_p2,
       transmission_7_p3, transmission_10_p2, transmission_10_p3;

  // Transmission_Gate transmission_1: pin names not known; wires that end beside it: in_3, transmission_1_p2, transmission_1_p3, out_15
  // Transmission_Gate transmission_2: pin names not known; wires that end beside it: in_4, transmission_1_p2, transmission_1_p3, out_16
  // Transmission_Gate transmission_3: pin names not known; wires that end beside it: in_5, transmission_1_p2, transmission_1_p3, out_17
  // Transmission_Gate transmission_4: pin names not known; wires that end beside it: in_6, transmission_4_p2, transmission_4_p3, out_15
  // Transmission_Gate transmission_5: pin names not known; wires that end beside it: in_7, transmission_4_p2, transmission_4_p3, out_16
  // Transmission_Gate transmission_6: pin names not known; wires that end beside it: in_8, transmission_4_p2, transmission_4_p3, out_17
  // Transmission_Gate transmission_7: pin names not known; wires that end beside it: in_9, transmission_7_p2, transmission_7_p3, out_15
  // Transmission_Gate transmission_8: pin names not known; wires that end beside it: in_10, transmission_7_p2, transmission_7_p3, out_16
  // Transmission_Gate transmission_9: pin names not known; wires that end beside it: in_11, transmission_7_p2, transmission_7_p3, out_17
  // Transmission_Gate transmission_10: pin names not known; wires that end beside it: in_12, transmission_10_p2, transmission_10_p3, out_15
  // Transmission_Gate transmission_11: pin names not known; wires that end beside it: in_13, transmission_10_p2, transmission_10_p3, out_16
  // Transmission_Gate transmission_12: pin names not known; wires that end beside it: in_14, transmission_10_p2, transmission_10_p3, out_17
  not not_1 (transmission_1_p2, transmission_1_p3);
  not not_2 (transmission_4_p2, transmission_4_p3);
  not not_3 (transmission_7_p2, transmission_7_p3);
  not not_4 (transmission_10_p2, transmission_10_p3);
  decoder_2_4 decoder_2_4_1 (
    .in_2(in_1), .in_1(in_2), .out_3(transmission_1_p3), .out_4(transmission_4_p3),
    .out_5(transmission_7_p3), .out_6(transmission_10_p3));
endmodule

module decoder_2_4 (
  input  in_1,
  input  in_2,
  output out_3,
  output out_4,
  output out_5,
  output out_6
);

  wire not_1_out, not_2_out, not_3_out;

  not not_1 (not_1_out, in_2);
  not not_2 (not_2_out, in_1);
  not not_3 (not_3_out, in_1);
  and and_1 (out_3, not_1_out, not_2_out);
  and and_2 (out_4, not_1_out, in_1);
  and and_3 (out_5, in_2, not_3_out);
  and and_4 (out_6, in_2, in_1);
endmodule

module sel_3bits_4_1_gates (
  input  in_1,
  input  in_2,
  input  in_3,
  input  in_4,
  input  in_5,
  input  in_6,
  input  in_7,
  input  in_8,
  input  in_9,
  input  in_10,
  input  in_11,
  input  in_12,
  input  in_13,
  input  in_14,
  output out_15,
  output out_16,
  output out_17
);

  wire and_1_out, and_2_out, and_3_out, and_4_out, and_5_out, and_6_out, and_7_out, and_8_out, and_9_out,
       and_10_out, and_11_out, and_12_out, decoder_2_4_1_out_3, decoder_2_4_1_out_4, decoder_2_4_1_out_5,
       decoder_2_4_1_out_6;

  decoder_2_4 decoder_2_4_1 (
    .in_2(in_1), .in_1(in_2), .out_3(decoder_2_4_1_out_3), .out_4(decoder_2_4_1_out_4),
    .out_5(decoder_2_4_1_out_5), .out_6(decoder_2_4_1_out_6));
  and and_1 (and_1_out, in_3, decoder_2_4_1_out_3);
  and and_2 (and_2_out, in_4, decoder_2_4_1_out_3);
  and and_3 (and_3_out, in_5, decoder_2_4_1_out_3);
  and and_4 (and_4_out, in_6, decoder_2_4_1_out_4);
  and and_5 (and_5_out, in_7, decoder_2_4_1_out_4);
  and and_6 (and_6_out, in_8, decoder_2_4_1_out_4);
  and and_7 (and_7_out, in_9, decoder_2_4_1_out_5);
  and and_8 (and_8_out, in_10, decoder_2_4_1_out_5);
  and and_9 (and_9_out, in_11, decoder_2_4_1_out_5);
  and and_10 (and_10_out, in_12, decoder_2_4_1_out_6);
  and and_11 (and_11_out, in_13, decoder_2_4_1_out_6);
  and and_12 (and_12_out, in_14, decoder_2_4_1_out_6);
  or or_1 (out_15, and_1_out, and_4_out, and_7_out, and_10_out);
  or or_2 (out_16, and_2_out, and_5_out, and_8_out, and_11_out);
  or or_3 (out_17, and_3_out, and_6_out, and_9_out, and_12_out);
endmodule

module sel_1bits_2_1_gates (
  input  in_1,
  input  in_2,
  input  in_3,
  output out_4
);

  wire not_1_out;

  not not_1 (not_1_out, in_1);
  and and_1 (out_4, in_2, not_1_out);
  and and_2 (out_4, in_1, in_3);
endmodule
