// Logisim project XORCrystal.circ as structural Verilog: 1 circuit, main circuit main
module main (
  input  in_1,
  input  in_2,
  input  in_3,
  input  in_4,
  input  in_5,
  input  in_6,
  input  in_7,
  input  in_8,
  output out_9,
  output out_10
);

  wire and_1_out, and_2_out, nand_1_out, nand_2_out, not_1_out, not_2_out, transistor_1_out,
       transistor_2_out, transistor_3_out;

  and and_1 (and_1_out, in_3, in_4);
  nand nand_1 (nand_1_out, in_3, in_3);
  and and_2 (and_2_out, in_7, in_8);
  nand nand_2 (nand_2_out, in_7, in_7);
  nor nor_1 (out_9, and_1_out, nand_1_out);
  or or_1 (out_10, and_2_out, nand_2_out);
  not not_1 (not_1_out, in_1);
  not not_2 (not_2_out, in_6);
  Transistor transistor_1 (.in(1'b1), .out(transistor_1_out), .gate(not_1_out));
  Transistor transistor_2 (.in(transistor_1_out), .out(transistor_2_out), .gate(not_2_out));
  Transistor transistor_3 (.in(1'b1), .out(transistor_3_out), .gate(in_1));
  Transistor transistor_4 (.in(transistor_3_out), .out(transistor_2_out), .gate(in_6));
  // Transmission_Gate transmission_1: pin names not known; wires that end beside it: transistor_2_out, 1'b1, 1'b0, in_2, in_5

  // Notes on the sheet:
  //   XOR
  //   XAND
endmodule
