// Logisim project Zeit.circ as structural Verilog
module SR_Latch (
  input  in_1,
  input  in_2,
  output Q,
  output Q_
);

  wire dipswitch_1_sw1, dipswitch_1_sw2, nor_3_out, nor_4_out;

  DipSwitch dipswitch_1 (.sw1(dipswitch_1_sw1), .sw2(dipswitch_1_sw2));  // open: sw3, sw4, sw5, sw6, sw7, sw8
  nor nor_1 (Q, in_1, Q_);
  nor nor_2 (Q_, Q, in_2);
  nor nor_3 (nor_3_out, dipswitch_1_sw1, nor_4_out);
  nor nor_4 (nor_4_out, nor_3_out, dipswitch_1_sw1);

  // Notes on the sheet:
  //   Q
  //   Q_
endmodule

module D_Latch (
  input  in_1,
  input  in_2,
  output out_3
);

  wire and_1_out, and_2_out, and_3_out, and_4_out, and_5_out, not_1_out, not_2_out, not_3_out, or_1_out,
       sr_latch_2_q_, undriven, undriven_2, undriven_3, xor_1_out;

  or or_1 (or_1_out, undriven, and_5_out);
  not not_1 (not_1_out, or_1_out);
  not not_2 (not_2_out, in_1);
  not not_3 (not_3_out, not_1_out);
  and and_1 (and_1_out, in_1, in_2);
  and and_2 (and_2_out, in_2, not_2_out);
  and and_3 (and_3_out, not_1_out, undriven_3);
  and and_4 (and_4_out, undriven_3, not_3_out);
  SR_Latch sr_latch_1 (.in_2(and_2_out), .in_1(and_1_out), .Q_(out_3));  // open: Q
  SR_Latch sr_latch_2 (.in_2(and_4_out), .in_1(and_3_out), .Q_(sr_latch_2_q_));  // open: Q
  xor xor_1 (xor_1_out, undriven_2, sr_latch_2_q_);
  and and_5 (and_5_out, xor_1_out, sr_latch_2_q_);

  // Notes on the sheet:
  //   RST
  //   RST
  //   Q
  //   Q
endmodule

module D_FF (
  input  in_1,
  input  in_2,
  output out_3
);

  wire d_latch_1_out_3, d_latch_2_out_3, d_latch_4_out_3, not_1_out, not_2_out, not_3_out, undriven,
       undriven_2;

  not not_1 (not_1_out, in_2);
  not not_2 (not_2_out, undriven_2);
  D_Latch d_latch_1 (.in_2(not_1_out), .in_1(in_1), .out_3(d_latch_1_out_3));
  D_Latch d_latch_2 (.in_2(not_2_out), .in_1(undriven), .out_3(d_latch_2_out_3));
  D_Latch d_latch_3 (.in_2(in_2), .in_1(d_latch_1_out_3), .out_3(out_3));
  not not_3 (not_3_out, d_latch_4_out_3);
  D_Latch d_latch_4 (.in_2(undriven_2), .in_1(d_latch_2_out_3), .out_3(d_latch_4_out_3));

  // Notes on the sheet:
  //   RST
endmodule

module D_FF_rst (
  input  in_1,
  input  in_2,
  input  in_3,
  output out_4
);

  wire and_1_out, d_latch_1_out_3, not_1_out, not_2_out;

  not not_1 (not_1_out, in_1);
  not not_2 (not_2_out, in_3);
  and and_1 (and_1_out, not_1_out, in_2);
  D_Latch d_latch_1 (.in_2(not_2_out), .in_1(and_1_out), .out_3(d_latch_1_out_3));
  D_Latch d_latch_2 (.in_2(in_3), .in_1(d_latch_1_out_3), .out_3(out_4));
endmodule

module D_FF_EN (
  input  in_1,
  input  EN,
  input  in_3,
  output out_4
);

  wire and_1_out;

  and and_1 (and_1_out, EN, in_3);
  D_FF d_ff_1 (.in_1(in_1), .in_2(and_1_out), .out_3(out_4));
endmodule

module register_4bits (
  input  in_1,
  input  in_2
);

  wire d_ff_rst_1_out_4, d_ff_rst_2_out_4, d_ff_rst_3_out_4, d_ff_rst_4_out_4, decoder_7segments_i_1_out_5,
       decoder_7segments_i_1_out_6, decoder_7segments_i_1_out_7, decoder_7segments_i_1_out_8,
       decoder_7segments_i_1_out_9, decoder_7segments_i_1_out_10, decoder_7segments_i_1_out_11,
       dipswitch_1_sw1, dipswitch_1_sw2, dipswitch_1_sw3, dipswitch_1_sw4;

  DipSwitch dipswitch_1 (
    .sw1(dipswitch_1_sw1), .sw2(dipswitch_1_sw2), .sw3(dipswitch_1_sw3), .sw4(dipswitch_1_sw4));  // open: sw5, sw6, sw7, sw8
  D_FF_rst d_ff_rst_1 (.in_1(in_2), .in_2(dipswitch_1_sw1), .in_3(in_1), .out_4(d_ff_rst_1_out_4));
  D_FF_rst d_ff_rst_2 (.in_1(in_2), .in_2(dipswitch_1_sw2), .in_3(in_1), .out_4(d_ff_rst_2_out_4));
  D_FF_rst d_ff_rst_3 (.in_1(in_2), .in_2(dipswitch_1_sw3), .in_3(in_1), .out_4(d_ff_rst_3_out_4));
  D_FF_rst d_ff_rst_4 (.in_1(in_2), .in_2(dipswitch_1_sw4), .in_3(in_1), .out_4(d_ff_rst_4_out_4));
  decoder_7segments_i decoder_7segments_i_1 (
    .in_1(d_ff_rst_1_out_4), .in_2(d_ff_rst_2_out_4), .in_3(d_ff_rst_3_out_4), .in_4(d_ff_rst_4_out_4),
    .out_5(decoder_7segments_i_1_out_5), .out_6(decoder_7segments_i_1_out_6),
    .out_7(decoder_7segments_i_1_out_7), .out_8(decoder_7segments_i_1_out_8),
    .out_9(decoder_7segments_i_1_out_9), .out_10(decoder_7segments_i_1_out_10),
    .out_11(decoder_7segments_i_1_out_11));
  _7_Segment_Display u_7_segment_display_1 (
    .g(decoder_7segments_i_1_out_5), .f(decoder_7segments_i_1_out_6), .a(decoder_7segments_i_1_out_7),
    .b(decoder_7segments_i_1_out_8), .e(decoder_7segments_i_1_out_9), .d(decoder_7segments_i_1_out_10),
    .c(decoder_7segments_i_1_out_11));  // open: dp
endmodule

module decoder3_8 (
  input  in_1,
  input  in_2,
  input  in_3,
  output out_4,
  output out_5,
  output out_6,
  output out_7,
  output out_8,
  output out_9,
  output out_10,
  output out_11
);

  wire not_1_out, not_2_out, not_3_out;

  not not_1 (not_1_out, in_1);
  not not_2 (not_2_out, in_2);
  not not_3 (not_3_out, in_3);
  and and_1 (out_4, not_1_out, not_2_out, not_3_out);
  and and_2 (out_5, in_1, not_2_out, not_3_out);
  and and_3 (out_6, not_1_out, in_2, not_3_out);
  and and_4 (out_7, in_1, in_2, not_3_out);
  and and_5 (out_8, not_1_out, not_2_out, in_3);
  and and_6 (out_9, in_1, not_2_out, in_3);
  and and_7 (out_10, not_1_out, in_2, in_3);
  and and_8 (out_11, in_1, in_2, in_3);
endmodule

module decoder4_16 (
  input  in_1,
  input  in_2,
  input  in_3,
  input  in_4,
  output out_5,
  output out_6,
  output out_7,
  output out_8,
  output out_9,
  output out_10,
  output out_11,
  output out_12,
  output out_13,
  output out_14,
  output out_15,
  output out_16,
  output out_17,
  output out_18,
  output out_19,
  output out_20
);

  wire and_1_out, and_2_out, and_3_out, and_4_out, and_5_out, and_6_out, decoder3_8_1_out_4,
       decoder3_8_2_out_4, not_1_out;

  not not_1 (not_1_out, in_4);
  and and_1 (and_1_out, in_1, not_1_out);
  and and_2 (and_2_out, in_2, not_1_out);
  and and_3 (and_3_out, in_3, not_1_out);
  and and_4 (and_4_out, in_4, in_1);
  and and_5 (and_5_out, in_4, in_2);
  and and_6 (and_6_out, in_4, in_3);
  decoder3_8 decoder3_8_1 (
    .in_1(and_1_out), .in_2(and_2_out), .in_3(and_3_out), .out_4(decoder3_8_1_out_4), .out_5(out_6),
    .out_6(out_7), .out_7(out_8), .out_8(out_9), .out_9(out_10), .out_10(out_11), .out_11(out_12));
  decoder3_8 decoder3_8_2 (
    .in_1(and_4_out), .in_2(and_5_out), .in_3(and_6_out), .out_4(decoder3_8_2_out_4), .out_5(out_14),
    .out_6(out_15), .out_7(out_16), .out_8(out_17), .out_9(out_18), .out_10(out_19), .out_11(out_20));
  and and_7 (out_5, not_1_out, decoder3_8_1_out_4);
  and and_8 (out_13, in_4, decoder3_8_2_out_4);
endmodule

module decoder_7segments_i (
  input  in_1,
  input  in_2,
  input  in_3,
  input  in_4,
  output out_5,
  output out_6,
  output out_7,
  output out_8,
  output out_9,
  output out_10,
  output out_11
);

  wire button_1_out, button_2_out, button_3_out, button_4_out, button_5_out, button_6_out, button_7_out,
       button_8_out, decoder4_16_1_out_5, decoder4_16_1_out_6, decoder4_16_1_out_7, decoder4_16_1_out_8,
       decoder4_16_1_out_9, decoder4_16_1_out_10, decoder4_16_1_out_11, decoder4_16_1_out_12,
       decoder4_16_1_out_13, decoder4_16_1_out_14, decoder4_16_1_out_15, decoder4_16_1_out_16,
       decoder4_16_1_out_17, decoder4_16_1_out_18, decoder4_16_1_out_19, decoder4_16_1_out_20;

  decoder4_16 decoder4_16_1 (
    .in_1(in_1), .in_2(in_2), .in_3(in_3), .in_4(in_4), .out_5(decoder4_16_1_out_5),
    .out_6(decoder4_16_1_out_6), .out_7(decoder4_16_1_out_7), .out_8(decoder4_16_1_out_8),
    .out_9(decoder4_16_1_out_9), .out_10(decoder4_16_1_out_10), .out_11(decoder4_16_1_out_11),
    .out_12(decoder4_16_1_out_12), .out_13(decoder4_16_1_out_13), .out_14(decoder4_16_1_out_14),
    .out_15(decoder4_16_1_out_15), .out_16(decoder4_16_1_out_16), .out_17(decoder4_16_1_out_17),
    .out_18(decoder4_16_1_out_18), .out_19(decoder4_16_1_out_19), .out_20(decoder4_16_1_out_20));
  or or_1 (out_5, decoder4_16_1_out_7, decoder4_16_1_out_8, decoder4_16_1_out_9, decoder4_16_1_out_10, decoder4_16_1_out_11, decoder4_16_1_out_13, decoder4_16_1_out_14, decoder4_16_1_out_15, decoder4_16_1_out_16, decoder4_16_1_out_18, decoder4_16_1_out_19, decoder4_16_1_out_20);
  or or_2 (out_6, decoder4_16_1_out_5, decoder4_16_1_out_9, decoder4_16_1_out_10, decoder4_16_1_out_11, decoder4_16_1_out_13, decoder4_16_1_out_14, decoder4_16_1_out_15, decoder4_16_1_out_16, decoder4_16_1_out_17, decoder4_16_1_out_19, decoder4_16_1_out_20);
  or or_3 (out_7, decoder4_16_1_out_5, decoder4_16_1_out_7, decoder4_16_1_out_8, decoder4_16_1_out_10, decoder4_16_1_out_11, decoder4_16_1_out_12, decoder4_16_1_out_13, decoder4_16_1_out_14, decoder4_16_1_out_15, decoder4_16_1_out_17, decoder4_16_1_out_19, decoder4_16_1_out_20);
  or or_4 (out_8, decoder4_16_1_out_5, decoder4_16_1_out_6, decoder4_16_1_out_7, decoder4_16_1_out_8, decoder4_16_1_out_9, decoder4_16_1_out_12, decoder4_16_1_out_13, decoder4_16_1_out_14, decoder4_16_1_out_15, decoder4_16_1_out_18);
  or or_5 (out_9, decoder4_16_1_out_5, decoder4_16_1_out_7, decoder4_16_1_out_11, decoder4_16_1_out_13, decoder4_16_1_out_20, decoder4_16_1_out_15, decoder4_16_1_out_16, decoder4_16_1_out_17, decoder4_16_1_out_18, decoder4_16_1_out_19);
  or or_6 (out_10, decoder4_16_1_out_5, decoder4_16_1_out_7, decoder4_16_1_out_8, decoder4_16_1_out_10, decoder4_16_1_out_11, decoder4_16_1_out_13, decoder4_16_1_out_14, decoder4_16_1_out_16, decoder4_16_1_out_17, decoder4_16_1_out_18, decoder4_16_1_out_19);
  or or_7 (out_11, decoder4_16_1_out_5, decoder4_16_1_out_6, decoder4_16_1_out_8, decoder4_16_1_out_9, decoder4_16_1_out_10, decoder4_16_1_out_11, decoder4_16_1_out_12, decoder4_16_1_out_13, decoder4_16_1_out_14, decoder4_16_1_out_15, decoder4_16_1_out_16, decoder4_16_1_out_18);
  _7_Segment_Display u_7_segment_display_1 (
    .g(out_5), .f(out_6), .a(out_7), .b(out_8), .e(out_9), .d(out_10), .c(out_11));  // open: dp
  Button button_1 (.out(button_1_out));
  Button button_2 (.out(button_2_out));
  Button button_3 (.out(button_3_out));
  Button button_4 (.out(button_4_out));
  _7_Segment_Display u_7_segment_display_2 (
    .g(button_4_out), .f(button_3_out), .a(button_2_out), .b(button_1_out), .e(button_5_out),
    .d(button_6_out), .c(button_7_out), .dp(button_8_out));
  Button button_5 (.out(button_5_out));
  Button button_6 (.out(button_6_out));
  Button button_7 (.out(button_7_out));
  Button button_8 (.out(button_8_out));

  // Notes on the sheet:
  //    0
  //   1
  //   2
  //   3
  //   4
  //   5
  //   6
  //   7
  //   8
  //   9
  //   A
  //   b
  //   C
  //   d
  //   E
  //   F
endmodule

module counter_4bits (
  input  in_1,
  input  in_2
);

  wire d_ff_rst_1_out_4, d_ff_rst_2_out_4, d_ff_rst_3_out_4, d_ff_rst_4_out_4, decoder_7segments_i_1_out_5,
       decoder_7segments_i_1_out_6, decoder_7segments_i_1_out_7, decoder_7segments_i_1_out_8,
       decoder_7segments_i_1_out_9, decoder_7segments_i_1_out_10, decoder_7segments_i_1_out_11,
       fulladder_36_1_count, fulladder_36_1_sum, fulladder_36_2_count, fulladder_36_2_sum,
       fulladder_36_3_count, fulladder_36_3_sum, fulladder_36_4_sum;

  fulladder_36 fulladder_36_1 (
    .in_1(d_ff_rst_1_out_4), .in_2(1'b1), .in_3(1'b0), .Sum(fulladder_36_1_sum), .Count(fulladder_36_1_count));
  fulladder_36 fulladder_36_2 (
    .in_1(d_ff_rst_2_out_4), .in_2(1'b0), .in_3(fulladder_36_1_count), .Sum(fulladder_36_2_sum),
    .Count(fulladder_36_2_count));
  fulladder_36 fulladder_36_3 (
    .in_1(d_ff_rst_3_out_4), .in_2(1'b0), .in_3(fulladder_36_2_count), .Sum(fulladder_36_3_sum),
    .Count(fulladder_36_3_count));
  fulladder_36 fulladder_36_4 (
    .in_1(d_ff_rst_4_out_4), .in_2(1'b0), .in_3(fulladder_36_3_count), .Sum(fulladder_36_4_sum));  // open: Count
  D_FF_rst d_ff_rst_1 (.in_1(in_1), .in_2(fulladder_36_1_sum), .in_3(in_2), .out_4(d_ff_rst_1_out_4));
  D_FF_rst d_ff_rst_2 (.in_1(in_1), .in_2(fulladder_36_2_sum), .in_3(in_2), .out_4(d_ff_rst_2_out_4));
  D_FF_rst d_ff_rst_3 (.in_1(in_1), .in_2(fulladder_36_3_sum), .in_3(in_2), .out_4(d_ff_rst_3_out_4));
  D_FF_rst d_ff_rst_4 (.in_1(in_1), .in_2(fulladder_36_4_sum), .in_3(in_2), .out_4(d_ff_rst_4_out_4));
  decoder_7segments_i decoder_7segments_i_1 (
    .in_1(d_ff_rst_1_out_4), .in_2(d_ff_rst_2_out_4), .in_3(d_ff_rst_3_out_4), .in_4(d_ff_rst_4_out_4),
    .out_5(decoder_7segments_i_1_out_5), .out_6(decoder_7segments_i_1_out_6),
    .out_7(decoder_7segments_i_1_out_7), .out_8(decoder_7segments_i_1_out_8),
    .out_9(decoder_7segments_i_1_out_9), .out_10(decoder_7segments_i_1_out_10),
    .out_11(decoder_7segments_i_1_out_11));
  _7_Segment_Display u_7_segment_display_1 (
    .g(decoder_7segments_i_1_out_5), .f(decoder_7segments_i_1_out_6), .a(decoder_7segments_i_1_out_7),
    .b(decoder_7segments_i_1_out_8), .e(decoder_7segments_i_1_out_9), .d(decoder_7segments_i_1_out_10),
    .c(decoder_7segments_i_1_out_11));  // open: dp
endmodule

module halfadder (
  input  in_1,
  input  in_2,
  output out_3,
  output out_4
);

  xor xor_1 (out_3, in_1, in_2);
  and and_1 (out_4, in_1, in_2);

  // Notes on the sheet:
  //   S
  //   C
endmodule

module fulladder_36 (
  input  in_1,
  input  in_2,
  input  in_3,
  output Sum,
  output Count
);

  wire halfadder_1_out_3, halfadder_1_out_4, halfadder_2_out_4;

  halfadder halfadder_1 (.in_1(in_1), .in_2(in_2), .out_3(halfadder_1_out_3), .out_4(halfadder_1_out_4));
  halfadder halfadder_2 (.in_1(halfadder_1_out_3), .in_2(in_3), .out_3(Sum), .out_4(halfadder_2_out_4));
  or or_1 (Count, halfadder_2_out_4, halfadder_1_out_4);

  // Notes on the sheet:
  //   But this is not a #T(36) fulladder, this is just a fulladder made of two  halfadder
endmodule

module array_sum (
  input  in_1,
  input  in_2
);

  wire decoder_7segments_i_1_out_5, decoder_7segments_i_1_out_6, decoder_7segments_i_1_out_7,
       decoder_7segments_i_1_out_8, decoder_7segments_i_1_out_9, decoder_7segments_i_1_out_10,
       decoder_7segments_i_1_out_11, decoder_7segments_i_2_out_5, decoder_7segments_i_2_out_6,
       decoder_7segments_i_2_out_7, decoder_7segments_i_2_out_8, decoder_7segments_i_2_out_9,
       decoder_7segments_i_2_out_10, decoder_7segments_i_2_out_11, fulladder_36_1_count, fulladder_36_1_sum,
       fulladder_36_2_count, fulladder_36_2_sum, fulladder_36_3_count, fulladder_36_3_sum,
       fulladder_36_4_count, fulladder_36_4_sum, fulladder_36_5_count, fulladder_36_5_sum,
       fulladder_36_6_count, fulladder_36_6_sum, fulladder_36_7_count, fulladder_36_7_sum,
       fulladder_36_8_sum, fulladder_36_9_count, fulladder_36_9_sum, fulladder_36_10_count,
       fulladder_36_10_sum, fulladder_36_11_count, fulladder_36_11_sum, fulladder_36_12_count,
       fulladder_36_12_sum, fulladder_36_13_count, fulladder_36_13_sum, fulladder_36_14_count,
       fulladder_36_14_sum, fulladder_36_15_count, fulladder_36_15_sum, fulladder_36_16_sum;
  wire [7:0] d_ff_rst_1_out_4, d_ff_rst_9_out_4;

  fulladder_36 fulladder_36_1 (
    .in_1(d_ff_rst_1_out_4[0]), .in_2(1'b1), .in_3(1'b0), .Sum(fulladder_36_1_sum),
    .Count(fulladder_36_1_count));
  fulladder_36 fulladder_36_2 (
    .in_1(d_ff_rst_1_out_4[1]), .in_2(1'b0), .in_3(fulladder_36_1_count), .Sum(fulladder_36_2_sum),
    .Count(fulladder_36_2_count));
  fulladder_36 fulladder_36_3 (
    .in_1(d_ff_rst_1_out_4[2]), .in_2(1'b0), .in_3(fulladder_36_2_count), .Sum(fulladder_36_3_sum),
    .Count(fulladder_36_3_count));
  fulladder_36 fulladder_36_4 (
    .in_1(d_ff_rst_1_out_4[3]), .in_2(1'b0), .in_3(fulladder_36_3_count), .Sum(fulladder_36_4_sum),
    .Count(fulladder_36_4_count));
  fulladder_36 fulladder_36_5 (
    .in_1(d_ff_rst_1_out_4[4]), .in_2(1'b0), .in_3(fulladder_36_4_count), .Sum(fulladder_36_5_sum),
    .Count(fulladder_36_5_count));
  fulladder_36 fulladder_36_6 (
    .in_1(d_ff_rst_1_out_4[5]), .in_2(1'b0), .in_3(fulladder_36_5_count), .Sum(fulladder_36_6_sum),
    .Count(fulladder_36_6_count));
  fulladder_36 fulladder_36_7 (
    .in_1(d_ff_rst_1_out_4[6]), .in_2(1'b0), .in_3(fulladder_36_6_count), .Sum(fulladder_36_7_sum),
    .Count(fulladder_36_7_count));
  fulladder_36 fulladder_36_8 (
    .in_1(d_ff_rst_1_out_4[7]), .in_2(1'b0), .in_3(fulladder_36_7_count), .Sum(fulladder_36_8_sum));  // open: Count
  D_FF_rst d_ff_rst_1 (.in_1(in_1), .in_2(fulladder_36_1_sum), .in_3(in_2), .out_4(d_ff_rst_1_out_4[0]));
  D_FF_rst d_ff_rst_2 (.in_1(in_1), .in_2(fulladder_36_2_sum), .in_3(in_2), .out_4(d_ff_rst_1_out_4[1]));
  D_FF_rst d_ff_rst_3 (.in_1(in_1), .in_2(fulladder_36_3_sum), .in_3(in_2), .out_4(d_ff_rst_1_out_4[2]));
  D_FF_rst d_ff_rst_4 (.in_1(in_1), .in_2(fulladder_36_4_sum), .in_3(in_2), .out_4(d_ff_rst_1_out_4[3]));
  D_FF_rst d_ff_rst_5 (.in_1(in_1), .in_2(fulladder_36_5_sum), .in_3(in_2), .out_4(d_ff_rst_1_out_4[4]));
  D_FF_rst d_ff_rst_6 (.in_1(in_1), .in_2(fulladder_36_6_sum), .in_3(in_2), .out_4(d_ff_rst_1_out_4[5]));
  D_FF_rst d_ff_rst_7 (.in_1(in_1), .in_2(fulladder_36_7_sum), .in_3(in_2), .out_4(d_ff_rst_1_out_4[6]));
  D_FF_rst d_ff_rst_8 (.in_1(in_1), .in_2(fulladder_36_8_sum), .in_3(in_2), .out_4(d_ff_rst_1_out_4[7]));
  fulladder_36 fulladder_36_9 (
    .in_1(d_ff_rst_9_out_4[0]), .in_2(d_ff_rst_1_out_4[0]), .in_3(1'b0), .Sum(fulladder_36_9_sum),
    .Count(fulladder_36_9_count));
  fulladder_36 fulladder_36_10 (
    .in_1(d_ff_rst_9_out_4[1]), .in_2(d_ff_rst_1_out_4[1]), .in_3(fulladder_36_9_count),
    .Sum(fulladder_36_10_sum), .Count(fulladder_36_10_count));
  fulladder_36 fulladder_36_11 (
    .in_1(d_ff_rst_9_out_4[2]), .in_2(d_ff_rst_1_out_4[2]), .in_3(fulladder_36_10_count),
    .Sum(fulladder_36_11_sum), .Count(fulladder_36_11_count));
  fulladder_36 fulladder_36_12 (
    .in_1(d_ff_rst_9_out_4[3]), .in_2(d_ff_rst_1_out_4[3]), .in_3(fulladder_36_11_count),
    .Sum(fulladder_36_12_sum), .Count(fulladder_36_12_count));
  fulladder_36 fulladder_36_13 (
    .in_1(d_ff_rst_9_out_4[4]), .in_2(d_ff_rst_1_out_4[4]), .in_3(fulladder_36_12_count),
    .Sum(fulladder_36_13_sum), .Count(fulladder_36_13_count));
  fulladder_36 fulladder_36_14 (
    .in_1(d_ff_rst_9_out_4[5]), .in_2(d_ff_rst_1_out_4[5]), .in_3(fulladder_36_13_count),
    .Sum(fulladder_36_14_sum), .Count(fulladder_36_14_count));
  fulladder_36 fulladder_36_15 (
    .in_1(d_ff_rst_9_out_4[6]), .in_2(d_ff_rst_1_out_4[6]), .in_3(fulladder_36_14_count),
    .Sum(fulladder_36_15_sum), .Count(fulladder_36_15_count));
  fulladder_36 fulladder_36_16 (
    .in_1(d_ff_rst_9_out_4[7]), .in_2(d_ff_rst_1_out_4[7]), .in_3(fulladder_36_15_count),
    .Sum(fulladder_36_16_sum));  // open: Count
  D_FF_rst d_ff_rst_9 (.in_1(in_1), .in_2(fulladder_36_9_sum), .in_3(in_2), .out_4(d_ff_rst_9_out_4[0]));
  D_FF_rst d_ff_rst_10 (.in_1(in_1), .in_2(fulladder_36_10_sum), .in_3(in_2), .out_4(d_ff_rst_9_out_4[1]));
  D_FF_rst d_ff_rst_11 (.in_1(in_1), .in_2(fulladder_36_11_sum), .in_3(in_2), .out_4(d_ff_rst_9_out_4[2]));
  D_FF_rst d_ff_rst_12 (.in_1(in_1), .in_2(fulladder_36_12_sum), .in_3(in_2), .out_4(d_ff_rst_9_out_4[3]));
  D_FF_rst d_ff_rst_13 (.in_1(in_1), .in_2(fulladder_36_13_sum), .in_3(in_2), .out_4(d_ff_rst_9_out_4[4]));
  D_FF_rst d_ff_rst_14 (.in_1(in_1), .in_2(fulladder_36_14_sum), .in_3(in_2), .out_4(d_ff_rst_9_out_4[5]));
  D_FF_rst d_ff_rst_15 (.in_1(in_1), .in_2(fulladder_36_15_sum), .in_3(in_2), .out_4(d_ff_rst_9_out_4[6]));
  D_FF_rst d_ff_rst_16 (.in_1(in_1), .in_2(fulladder_36_16_sum), .in_3(in_2), .out_4(d_ff_rst_9_out_4[7]));
  decoder_7segments_i decoder_7segments_i_1 (
    .in_1(d_ff_rst_9_out_4[0]), .in_2(d_ff_rst_9_out_4[1]), .in_3(d_ff_rst_9_out_4[2]),
    .in_4(d_ff_rst_9_out_4[3]), .out_5(decoder_7segments_i_1_out_5), .out_6(decoder_7segments_i_1_out_6),
    .out_7(decoder_7segments_i_1_out_7), .out_8(decoder_7segments_i_1_out_8),
    .out_9(decoder_7segments_i_1_out_9), .out_10(decoder_7segments_i_1_out_10),
    .out_11(decoder_7segments_i_1_out_11));
  decoder_7segments_i decoder_7segments_i_2 (
    .in_1(d_ff_rst_9_out_4[4]), .in_2(d_ff_rst_9_out_4[5]), .in_3(d_ff_rst_9_out_4[6]),
    .in_4(d_ff_rst_9_out_4[7]), .out_5(decoder_7segments_i_2_out_5), .out_6(decoder_7segments_i_2_out_6),
    .out_7(decoder_7segments_i_2_out_7), .out_8(decoder_7segments_i_2_out_8),
    .out_9(decoder_7segments_i_2_out_9), .out_10(decoder_7segments_i_2_out_10),
    .out_11(decoder_7segments_i_2_out_11));
  _7_Segment_Display u_7_segment_display_1 (
    .g(decoder_7segments_i_2_out_5), .f(decoder_7segments_i_2_out_6), .a(decoder_7segments_i_2_out_7),
    .b(decoder_7segments_i_2_out_8), .e(decoder_7segments_i_2_out_9), .d(decoder_7segments_i_2_out_10),
    .c(decoder_7segments_i_2_out_11));  // open: dp
  _7_Segment_Display u_7_segment_display_2 (
    .g(decoder_7segments_i_1_out_5), .f(decoder_7segments_i_1_out_6), .a(decoder_7segments_i_1_out_7),
    .b(decoder_7segments_i_1_out_8), .e(decoder_7segments_i_1_out_9), .d(decoder_7segments_i_1_out_10),
    .c(decoder_7segments_i_1_out_11));  // open: dp
endmodule

module halfsubber (
  input  in_1,
  input  in_2,
  output out_3,
  output out_4
);

  xor xor_1 (out_3, in_1, in_2);
  and and_1 (out_4, out_3, in_2);

  // Notes on the sheet:
  //   A
  //   B
endmodule

module fullsubber (
  input  in_1,
  input  in_2,
  input  in_3,
  output out_4,
  output out_5
);

  wire halfsubber_1_out_3, halfsubber_1_out_4, halfsubber_2_out_4;

  halfsubber halfsubber_1 (.in_1(in_1), .in_2(in_2), .out_3(halfsubber_1_out_3), .out_4(halfsubber_1_out_4));
  halfsubber halfsubber_2 (.in_1(halfsubber_1_out_3), .in_2(in_3), .out_3(out_4), .out_4(halfsubber_2_out_4));
  or or_1 (out_5, halfsubber_1_out_4, halfsubber_2_out_4);
endmodule

module counter_8bits (
  input  in_1,
  input  in_2,
  output [7:0] out_3
);

  wire fulladder_36_1_count, fulladder_36_1_sum, fulladder_36_2_count, fulladder_36_2_sum,
       fulladder_36_3_count, fulladder_36_3_sum, fulladder_36_4_count, fulladder_36_4_sum,
       fulladder_36_5_count, fulladder_36_5_sum, fulladder_36_6_count, fulladder_36_6_sum,
       fulladder_36_7_sum, fulladder_36_8_sum;

  fulladder_36 fulladder_36_1 (
    .in_1(out_3[0]), .in_2(1'b1), .in_3(1'b0), .Sum(fulladder_36_1_sum), .Count(fulladder_36_1_count));
  fulladder_36 fulladder_36_2 (
    .in_1(out_3[1]), .in_2(1'b0), .in_3(fulladder_36_1_count), .Sum(fulladder_36_2_sum),
    .Count(fulladder_36_2_count));
  fulladder_36 fulladder_36_3 (
    .in_1(out_3[2]), .in_2(1'b0), .in_3(fulladder_36_2_count), .Sum(fulladder_36_3_sum),
    .Count(fulladder_36_3_count));
  fulladder_36 fulladder_36_4 (
    .in_1(out_3[3]), .in_2(1'b0), .in_3(fulladder_36_3_count), .Sum(fulladder_36_4_sum),
    .Count(fulladder_36_4_count));
  fulladder_36 fulladder_36_5 (
    .in_1(out_3[4]), .in_2(1'b0), .in_3(fulladder_36_4_count), .Sum(fulladder_36_5_sum),
    .Count(fulladder_36_5_count));
  fulladder_36 fulladder_36_6 (
    .in_1(out_3[5]), .in_2(1'b0), .in_3(fulladder_36_5_count), .Sum(fulladder_36_6_sum),
    .Count(fulladder_36_6_count));
  fulladder_36 fulladder_36_7 (
    .in_1(out_3[6]), .in_2(1'b0), .in_3(fulladder_36_6_count), .Sum(fulladder_36_7_sum), .Count(out_3[7]));
  fulladder_36 fulladder_36_8 (.in_1(out_3[7]), .in_2(1'b0), .in_3(out_3[7]), .Sum(fulladder_36_8_sum));  // open: Count
  D_FF_rst d_ff_rst_1 (.in_1(in_1), .in_2(fulladder_36_1_sum), .in_3(in_2), .out_4(out_3[0]));
  D_FF_rst d_ff_rst_2 (.in_1(in_1), .in_2(fulladder_36_2_sum), .in_3(in_2), .out_4(out_3[1]));
  D_FF_rst d_ff_rst_3 (.in_1(in_1), .in_2(fulladder_36_3_sum), .in_3(in_2), .out_4(out_3[2]));
  D_FF_rst d_ff_rst_4 (.in_1(in_1), .in_2(fulladder_36_4_sum), .in_3(in_2), .out_4(out_3[3]));
  D_FF_rst d_ff_rst_5 (.in_1(in_1), .in_2(fulladder_36_5_sum), .in_3(in_2), .out_4(out_3[4]));
  D_FF_rst d_ff_rst_6 (.in_1(in_1), .in_2(fulladder_36_6_sum), .in_3(in_2), .out_4(out_3[5]));
  D_FF_rst d_ff_rst_7 (.in_1(in_1), .in_2(fulladder_36_7_sum), .in_3(in_2), .out_4(out_3[6]));
  D_FF_rst d_ff_rst_8 (.in_1(in_1), .in_2(fulladder_36_8_sum), .in_3(in_2), .out_4(out_3[7]));
endmodule

module adder_plus1_8bits (
  input  [7:0] in_1,
  output [7:0] out_2
);

  wire fulladder_36_1_count, fulladder_36_2_count, fulladder_36_3_count, fulladder_36_4_count,
       fulladder_36_5_count, fulladder_36_6_count;

  fulladder_36 fulladder_36_1 (.in_1(in_1[0]), .in_2(1'b1), .in_3(1'b0), .Sum(out_2[0]), .Count(fulladder_36_1_count));
  fulladder_36 fulladder_36_2 (
    .in_1(in_1[1]), .in_2(1'b0), .in_3(fulladder_36_1_count), .Sum(out_2[1]), .Count(fulladder_36_2_count));
  fulladder_36 fulladder_36_3 (
    .in_1(in_1[2]), .in_2(1'b0), .in_3(fulladder_36_2_count), .Sum(out_2[2]), .Count(fulladder_36_3_count));
  fulladder_36 fulladder_36_4 (
    .in_1(in_1[3]), .in_2(1'b0), .in_3(fulladder_36_3_count), .Sum(out_2[3]), .Count(fulladder_36_4_count));
  fulladder_36 fulladder_36_5 (
    .in_1(in_1[4]), .in_2(1'b0), .in_3(fulladder_36_4_count), .Sum(out_2[4]), .Count(fulladder_36_5_count));
  fulladder_36 fulladder_36_6 (
    .in_1(in_1[5]), .in_2(1'b0), .in_3(fulladder_36_5_count), .Sum(out_2[5]), .Count(fulladder_36_6_count));
  fulladder_36 fulladder_36_7 (
    .in_1(in_1[6]), .in_2(1'b0), .in_3(fulladder_36_6_count), .Sum(out_2[6]), .Count(in_1[7]));
  fulladder_36 fulladder_36_8 (.in_1(in_1[7]), .in_2(1'b0), .in_3(in_1[7]), .Sum(out_2[7]));  // open: Count
endmodule

module electronic_clock (
);

  Clock clock_1 ();  // open: out
  _7_Segment_Display u_7_segment_display_1 ();  // open: g, f, a, b, e, d, c, dp
  _7_Segment_Display u_7_segment_display_2 ();  // open: g, f, a, b, e, d, c, dp
  _7_Segment_Display u_7_segment_display_3 ();  // open: g, f, a, b, e, d, c, dp
  _7_Segment_Display u_7_segment_display_4 ();  // open: g, f, a, b, e, d, c, dp
endmodule

module decoder_7segments (
  input  in_1,
  input  in_2,
  input  in_3,
  input  in_4,
  output out_5,
  output out_6,
  output out_7,
  output out_8,
  output out_9,
  output out_10,
  output out_11,
  output out_12
);

  wire button_1_out, button_2_out, button_3_out, button_4_out, button_5_out, button_6_out, button_7_out,
       button_8_out, decoder4_16_1_out_5, decoder4_16_1_out_6, decoder4_16_1_out_7, decoder4_16_1_out_8,
       decoder4_16_1_out_9, decoder4_16_1_out_10, decoder4_16_1_out_11, decoder4_16_1_out_12,
       decoder4_16_1_out_13, decoder4_16_1_out_14, not_1_out, not_2_out, not_3_out, not_4_out, not_5_out,
       not_6_out, not_7_out, not_8_out, not_9_out, not_10_out;

  Button button_1 (.out(button_1_out));
  Button button_2 (.out(button_2_out));
  Button button_3 (.out(button_3_out));
  Button button_4 (.out(button_4_out));
  Button button_5 (.out(button_5_out));
  Button button_6 (.out(button_6_out));
  Button button_7 (.out(button_7_out));
  Button button_8 (.out(button_8_out));
  _7_Segment_Display u_7_segment_display_1 (
    .g(button_4_out), .f(button_3_out), .a(button_2_out), .b(button_1_out), .e(button_5_out),
    .d(button_6_out), .c(button_7_out), .dp(button_8_out));
  decoder4_16 decoder4_16_1 (
    .in_1(in_1), .in_2(in_2), .in_3(in_3), .in_4(in_4), .out_5(decoder4_16_1_out_5),
    .out_6(decoder4_16_1_out_6), .out_7(decoder4_16_1_out_7), .out_8(decoder4_16_1_out_8),
    .out_9(decoder4_16_1_out_9), .out_10(decoder4_16_1_out_10), .out_11(decoder4_16_1_out_11),
    .out_12(decoder4_16_1_out_12), .out_13(decoder4_16_1_out_13), .out_14(decoder4_16_1_out_14));  // open: out_15, out_16, out_17, out_18, out_19, out_20
  or or_1 (out_5, decoder4_16_1_out_7, decoder4_16_1_out_8, decoder4_16_1_out_9, decoder4_16_1_out_10, decoder4_16_1_out_11, decoder4_16_1_out_13, decoder4_16_1_out_14);
  or or_2 (out_6, decoder4_16_1_out_5, decoder4_16_1_out_9, decoder4_16_1_out_10, decoder4_16_1_out_11, decoder4_16_1_out_13, decoder4_16_1_out_14);
  or or_3 (out_7, decoder4_16_1_out_5, decoder4_16_1_out_7, decoder4_16_1_out_8, decoder4_16_1_out_10, decoder4_16_1_out_11, decoder4_16_1_out_12, decoder4_16_1_out_13, decoder4_16_1_out_14);
  or or_4 (out_11, decoder4_16_1_out_5, decoder4_16_1_out_7, decoder4_16_1_out_8, decoder4_16_1_out_10, decoder4_16_1_out_11, decoder4_16_1_out_13, decoder4_16_1_out_14);
  or or_5 (out_8, decoder4_16_1_out_5, decoder4_16_1_out_6, decoder4_16_1_out_7, decoder4_16_1_out_8, decoder4_16_1_out_9, decoder4_16_1_out_12, decoder4_16_1_out_13, decoder4_16_1_out_14);
  or or_6 (out_12, decoder4_16_1_out_5, decoder4_16_1_out_7, decoder4_16_1_out_11, decoder4_16_1_out_13);
  not not_1 (not_1_out, decoder4_16_1_out_5);
  not not_2 (not_2_out, decoder4_16_1_out_6);
  not not_3 (not_3_out, decoder4_16_1_out_7);
  not not_4 (not_4_out, decoder4_16_1_out_8);
  not not_5 (not_5_out, decoder4_16_1_out_9);
  not not_6 (not_6_out, decoder4_16_1_out_10);
  not not_7 (not_7_out, decoder4_16_1_out_11);
  not not_8 (not_8_out, decoder4_16_1_out_12);
  not not_9 (not_9_out, decoder4_16_1_out_13);
  not not_10 (not_10_out, decoder4_16_1_out_14);
  or or_7 (out_10, decoder4_16_1_out_5, decoder4_16_1_out_6, decoder4_16_1_out_13, decoder4_16_1_out_8, decoder4_16_1_out_14, decoder4_16_1_out_9, decoder4_16_1_out_10, decoder4_16_1_out_11, decoder4_16_1_out_12);
  and and_1 (out_9, not_1_out, not_2_out, not_3_out, not_4_out, not_5_out, not_6_out, not_7_out, not_8_out, not_9_out, not_10_out);
  _7_Segment_Display u_7_segment_display_2 (
    .g(out_5), .f(out_6), .a(out_7), .b(out_8), .e(out_12), .d(out_11), .c(out_10), .dp(out_9));

  // Notes on the sheet:
  //   0
  //   1
  //   2
  //   3
  //   4
  //   5
  //   6
  //   7
  //   8
  //   9
endmodule
