// Logisim project comparer.circ as structural Verilog
module comparer_4bits (
  input  in_1,
  input  in_2,
  input  in_3,
  input  in_4,
  input  in_5,
  input  in_6,
  input  in_7,
  input  in_8
);

  wire and_1_out, not_1_out, not_2_out, not_3_out, not_4_out, xor_1_out, xor_2_out, xor_3_out, xor_4_out;

  xor xor_1 (xor_1_out, in_1, in_5);
  xor xor_2 (xor_2_out, in_2, in_6);
  xor xor_3 (xor_3_out, in_3, in_7);
  xor xor_4 (xor_4_out, in_4, in_8);
  not not_1 (not_1_out, xor_1_out);
  not not_2 (not_2_out, xor_2_out);
  not not_3 (not_3_out, xor_3_out);
  not not_4 (not_4_out, xor_4_out);
  and and_1 (and_1_out, not_1_out, not_2_out, not_3_out, not_4_out);
  LED led_1 (.in(and_1_out));
endmodule
